// Logisim project 32bitCPU.circ as structural Verilog: 24 circuits, main circuit main
module main (
);

  wire alu32_3_zero, and_1_out, and_2_out, clock_1_out, control_1_alusrc, control_1_branch,
       control_1_memread, control_1_memtoreg, control_1_memwrite, control_1_op0, control_1_op1,
       control_1_regdst, control_1_regwrite;
  wire [3:0] alucontrol_1_operation;
  wire [4:0] instructionsplitter_1_readreg1, instructionsplitter_1_readreg2, instructionsplitter_1_writereg,
       regdstmux_1_regout;
  wire [5:0] instructionsplitter_1_alucontrol, instructionsplitter_1_control;
  wire [15:0] instructionsplitter_1_immediate, signshrinker_1_out16, signshrinker_2_out16;
  wire [31:0] alu32_1_result, alu32_2_result, alu32_3_result, datamux_1_dataout, datamux_2_dataout,
       datamux_3_dataout, programcounter_1_pcout, ram_1_dout, registersblock_1_readdata1,
       registersblock_1_readdata2, rom_1_data, signextender_1_out32;

  SignShrinker signshrinker_1 (.In32(programcounter_1_pcout), .Out16(signshrinker_1_out16));
  ROM #(.addrWidth(16), .dataWidth(32)) rom_1 (.addr(signshrinker_1_out16), .data(rom_1_data));
  ProgramCounter programcounter_1 (.Clock(clock_1_out), .PCin(datamux_2_dataout), .PCout(programcounter_1_pcout));
  InstructionSplitter instructionsplitter_1 (
    .Instruction(rom_1_data), .Clock(clock_1_out), .ReadReg1(instructionsplitter_1_readreg1),
    .Control(instructionsplitter_1_control), .ReadReg2(instructionsplitter_1_readreg2),
    .WriteReg(instructionsplitter_1_writereg), .Immediate(instructionsplitter_1_immediate),
    .ALUControl(instructionsplitter_1_alucontrol));
  Clock #(.phaseOffset(1)) clock_1 (.out(clock_1_out));
  ALU32 alu32_1 (
    .Operation(4'b0010), .A(programcounter_1_pcout), .B(32'h1), .Result(alu32_1_result));  // open: Overflow, Zero
  Control control_1 (
    .OpCode(instructionsplitter_1_control), .RegDst(control_1_regdst), .ALUSrc(control_1_alusrc),
    .MemToReg(control_1_memtoreg), .RegWrite(control_1_regwrite), .MemRead(control_1_memread),
    .MemWrite(control_1_memwrite), .Branch(control_1_branch), .Op1(control_1_op1), .Op0(control_1_op0));
  RegDstMux regdstmux_1 (
    .RegDst(control_1_regdst), .Read(instructionsplitter_1_readreg2), .Write(instructionsplitter_1_writereg),
    .RegOut(regdstmux_1_regout));
  SignExtender signextender_1 (.In16(instructionsplitter_1_immediate), .Out32(signextender_1_out32));
  and and_1 (and_1_out, clock_1_out, control_1_regwrite);
  RegistersBlock registersblock_1 (
    .ReadReg1(instructionsplitter_1_readreg1), .ReadReg2(instructionsplitter_1_readreg2),
    .WriteReg(regdstmux_1_regout), .WriteData(datamux_3_dataout), .Clock(and_1_out),
    .ReadData1(registersblock_1_readdata1), .ReadData2(registersblock_1_readdata2));
  ALUControl alucontrol_1 (
    .Funct(instructionsplitter_1_alucontrol), .Op0(control_1_op0), .Op1(control_1_op1),
    .Operation(alucontrol_1_operation));
  ALU32 alu32_2 (
    .Operation(4'b0010), .A(alu32_1_result), .B(signextender_1_out32), .Result(alu32_2_result));  // open: Overflow, Zero
  DataMux datamux_1 (
    .Source(control_1_alusrc), .Data1(registersblock_1_readdata2), .Data2(signextender_1_out32),
    .DataOut(datamux_1_dataout));
  DataMux datamux_2 (.Source(and_2_out), .Data1(alu32_1_result), .Data2(alu32_2_result), .DataOut(datamux_2_dataout));
  and and_2 (and_2_out, control_1_branch, alu32_3_zero);
  ALU32 alu32_3 (
    .Operation(alucontrol_1_operation), .A(registersblock_1_readdata1), .B(datamux_1_dataout),
    .Zero(alu32_3_zero), .Result(alu32_3_result));  // open: Overflow
  DataMux datamux_3 (
    .Source(control_1_memtoreg), .Data1(ram_1_dout), .Data2(alu32_3_result), .DataOut(datamux_3_dataout));
  SignShrinker signshrinker_2 (.In32(alu32_3_result), .Out16(signshrinker_2_out16));
  RAM #(.addrWidth(16), .dataWidth(32), .\type ("nonvolatile")) ram_1 (
    .addr(signshrinker_2_out16), .we(control_1_memwrite), .oe(control_1_memread), .clk(clock_1_out),
    .din(registersblock_1_readdata2), .dout(ram_1_dout));

  // Notes on the sheet:
  //   contents of rom_1 (hex, n*v repeats v):
  //   8c080004 8c090005 1095020 ac0a0006 2 4
endmodule

module MUX2 (
  input  A,
  input  B,
  input  S,
  output X
);

  wire and_1_out, and_2_out, not_1_out;

  not not_1 (not_1_out, S);
  and and_1 (and_1_out, A, not_1_out);
  and and_2 (and_2_out, S, B);
  or or_1 (X, and_1_out, and_2_out);
endmodule

module Adder (
  input  CarryIn,
  input  A,
  input  B,
  output CarryOut,
  output Sum
);

  wire and_1_out, and_2_out, and_3_out, and_4_out, xor_1_out;

  and and_1 (and_1_out, CarryIn, B);
  ExactlyOne xor_1 (.out(xor_1_out), .in0(CarryIn), .in1(A), .in2(B));
  and and_2 (and_2_out, CarryIn, B, A);
  and and_3 (and_3_out, CarryIn, A);
  or or_1 (CarryOut, and_3_out, and_1_out, and_4_out);
  and and_4 (and_4_out, A, B);
  or or_2 (Sum, xor_1_out, and_2_out);
endmodule

module ALU1 (
  input  Ainvert,
  input  CarryIn,
  input  A,
  input  O2,
  input  O1,
  input  Binvert,
  input  B,
  input  Less,
  output Result,
  output CarryOut
);

  wire adder_1_sum, and_1_out, mux2_1_x, mux2_2_x, not_1_out, not_2_out, or_1_out;

  not not_1 (not_1_out, A);
  not not_2 (not_2_out, B);
  MUX2 mux2_1 (.A(A), .B(not_1_out), .S(Ainvert), .X(mux2_1_x));
  MUX2 mux2_2 (.A(B), .B(not_2_out), .S(Binvert), .X(mux2_2_x));
  Adder adder_1 (.A(mux2_1_x), .B(mux2_2_x), .CarryIn(CarryIn), .Sum(adder_1_sum), .CarryOut(CarryOut));
  and and_1 (and_1_out, mux2_1_x, mux2_2_x);
  or or_1 (or_1_out, mux2_1_x, mux2_2_x);
  MUX4 mux4_1 (.A(and_1_out), .B(or_1_out), .C(adder_1_sum), .D(Less), .S1(O1), .S2(O2), .X(Result));
endmodule

module MUX4 (
  input  A,
  input  B,
  input  C,
  input  D,
  input  S1,
  input  S2,
  output X
);

  wire and_1_out, and_2_out, and_3_out, and_4_out, not_1_out, not_2_out, not_3_out, not_4_out;

  not not_1 (not_1_out, S1);
  not not_2 (not_2_out, S2);
  not not_3 (not_3_out, S1);
  not not_4 (not_4_out, S2);
  and and_1 (and_1_out, A, not_1_out, not_2_out);
  and and_2 (and_2_out, B, not_3_out, S2);
  and and_3 (and_3_out, C, S1, not_4_out);
  and and_4 (and_4_out, D, S1, S2);
  or or_1 (X, and_1_out, and_2_out, and_3_out, and_4_out);
endmodule

module ALU32 (
  input  [3:0] Operation,
  input  [31:0] A,
  input  [31:0] B,
  output Zero,
  output Overflow,
  output [31:0] Result
);

  wire alu1_1_carryout, alu1_1_result, alu1_2_carryout, alu1_2_result, alu1_3_carryout, alu1_3_result,
       alu1_4_carryout, alu1_4_result, alu1_5_carryout, alu1_5_result, alu1_6_carryout, alu1_6_result,
       alu1_7_carryout, alu1_7_result, alu1_8_carryout, alu1_8_result, alu1_9_carryout, alu1_9_result,
       alu1_10_carryout, alu1_10_result, alu1_11_carryout, alu1_11_result, alu1_12_carryout, alu1_12_result,
       alu1_13_carryout, alu1_13_result, alu1_14_carryout, alu1_14_result, alu1_15_carryout, alu1_15_result,
       alu1_16_carryout, alu1_16_result, alu1_17_carryout, alu1_17_result, alu1_18_carryout, alu1_18_result,
       alu1_19_carryout, alu1_19_result, alu1_20_carryout, alu1_20_result, alu1_21_carryout, alu1_21_result,
       alu1_22_carryout, alu1_22_result, alu1_23_carryout, alu1_23_result, alu1_24_carryout, alu1_24_result,
       alu1_25_carryout, alu1_25_result, alu1_26_carryout, alu1_26_result, alu1_27_carryout, alu1_27_result,
       alu1_28_carryout, alu1_28_result, alu1_29_carryout, alu1_29_result, alu1_30_carryout, alu1_30_result,
       alu1_31_carryout, alu1_31_result, alu1_32_result, aluopconv_1_ainvert, aluopconv_1_binvert,
       aluopconv_1_o1, aluopconv_1_o2, bitconv1_1_b0, bitconv1_1_b1, bitconv1_1_b2, bitconv1_1_b3,
       bitconv1_1_b4, bitconv1_1_b5, bitconv1_1_b6, bitconv1_1_b7, bitconv1_1_b8, bitconv1_1_b9,
       bitconv1_1_b10, bitconv1_1_b11, bitconv1_1_b12, bitconv1_1_b13, bitconv1_1_b14, bitconv1_1_b15,
       bitconv1_1_b16, bitconv1_1_b17, bitconv1_1_b18, bitconv1_1_b19, bitconv1_1_b20, bitconv1_1_b21,
       bitconv1_1_b22, bitconv1_1_b23, bitconv1_1_b24, bitconv1_1_b25, bitconv1_1_b26, bitconv1_1_b27,
       bitconv1_1_b28, bitconv1_1_b29, bitconv1_1_b30, bitconv1_1_b31, bitconv1_2_b0, bitconv1_2_b1,
       bitconv1_2_b2, bitconv1_2_b3, bitconv1_2_b4, bitconv1_2_b5, bitconv1_2_b6, bitconv1_2_b7,
       bitconv1_2_b8, bitconv1_2_b9, bitconv1_2_b10, bitconv1_2_b11, bitconv1_2_b12, bitconv1_2_b13,
       bitconv1_2_b14, bitconv1_2_b15, bitconv1_2_b16, bitconv1_2_b17, bitconv1_2_b18, bitconv1_2_b19,
       bitconv1_2_b20, bitconv1_2_b21, bitconv1_2_b22, bitconv1_2_b23, bitconv1_2_b24, bitconv1_2_b25,
       bitconv1_2_b26, bitconv1_2_b27, bitconv1_2_b28, bitconv1_2_b29, bitconv1_2_b30, bitconv1_2_b31,
       or_1_out;

  BitConv1 bitconv1_1 (
    .Bit32(A), .B2(bitconv1_1_b2), .B3(bitconv1_1_b3), .B4(bitconv1_1_b4), .B5(bitconv1_1_b5),
    .B6(bitconv1_1_b6), .B7(bitconv1_1_b7), .B8(bitconv1_1_b8), .B9(bitconv1_1_b9), .B10(bitconv1_1_b10),
    .B11(bitconv1_1_b11), .B12(bitconv1_1_b12), .B13(bitconv1_1_b13), .B14(bitconv1_1_b14),
    .B0(bitconv1_1_b0), .B15(bitconv1_1_b15), .B16(bitconv1_1_b16), .B17(bitconv1_1_b17),
    .B18(bitconv1_1_b18), .B19(bitconv1_1_b19), .B20(bitconv1_1_b20), .B21(bitconv1_1_b21),
    .B22(bitconv1_1_b22), .B23(bitconv1_1_b23), .B24(bitconv1_1_b24), .B1(bitconv1_1_b1),
    .B25(bitconv1_1_b25), .B26(bitconv1_1_b26), .B27(bitconv1_1_b27), .B28(bitconv1_1_b28),
    .B29(bitconv1_1_b29), .B30(bitconv1_1_b30), .B31(bitconv1_1_b31));
  BitConv1 bitconv1_2 (
    .Bit32(B), .B2(bitconv1_2_b2), .B3(bitconv1_2_b3), .B4(bitconv1_2_b4), .B5(bitconv1_2_b5),
    .B6(bitconv1_2_b6), .B7(bitconv1_2_b7), .B8(bitconv1_2_b8), .B9(bitconv1_2_b9), .B10(bitconv1_2_b10),
    .B11(bitconv1_2_b11), .B12(bitconv1_2_b12), .B13(bitconv1_2_b13), .B14(bitconv1_2_b14),
    .B0(bitconv1_2_b0), .B15(bitconv1_2_b15), .B16(bitconv1_2_b16), .B17(bitconv1_2_b17),
    .B18(bitconv1_2_b18), .B19(bitconv1_2_b19), .B20(bitconv1_2_b20), .B21(bitconv1_2_b21),
    .B22(bitconv1_2_b22), .B23(bitconv1_2_b23), .B24(bitconv1_2_b24), .B1(bitconv1_2_b1),
    .B25(bitconv1_2_b25), .B26(bitconv1_2_b26), .B27(bitconv1_2_b27), .B28(bitconv1_2_b28),
    .B29(bitconv1_2_b29), .B30(bitconv1_2_b30), .B31(bitconv1_2_b31));
  ALUopConv aluopconv_1 (
    .ALUop(Operation), .Ainvert(aluopconv_1_ainvert), .Binvert(aluopconv_1_binvert), .O1(aluopconv_1_o1),
    .O2(aluopconv_1_o2));
  ALU1 alu1_1 (
    .A(bitconv1_1_b0), .B(bitconv1_2_b0), .Ainvert(aluopconv_1_ainvert), .Binvert(aluopconv_1_binvert),
    .Less(Overflow), .O1(aluopconv_1_o1), .O2(aluopconv_1_o2), .CarryOut(alu1_1_carryout),
    .Result(alu1_1_result));  // open: CarryIn
  ALU1 alu1_2 (
    .A(bitconv1_1_b1), .B(bitconv1_2_b1), .Ainvert(aluopconv_1_ainvert), .Binvert(aluopconv_1_binvert),
    .CarryIn(alu1_1_carryout), .O1(aluopconv_1_o1), .O2(aluopconv_1_o2), .CarryOut(alu1_2_carryout),
    .Result(alu1_2_result));  // open: Less
  ALU1 alu1_3 (
    .A(bitconv1_1_b2), .B(bitconv1_2_b2), .Ainvert(aluopconv_1_ainvert), .Binvert(aluopconv_1_binvert),
    .CarryIn(alu1_2_carryout), .O1(aluopconv_1_o1), .O2(aluopconv_1_o2), .CarryOut(alu1_3_carryout),
    .Result(alu1_3_result));  // open: Less
  ALU1 alu1_4 (
    .A(bitconv1_1_b3), .B(bitconv1_2_b3), .Ainvert(aluopconv_1_ainvert), .Binvert(aluopconv_1_binvert),
    .CarryIn(alu1_3_carryout), .O1(aluopconv_1_o1), .O2(aluopconv_1_o2), .CarryOut(alu1_4_carryout),
    .Result(alu1_4_result));  // open: Less
  ALU1 alu1_5 (
    .A(bitconv1_1_b4), .B(bitconv1_2_b4), .Ainvert(aluopconv_1_ainvert), .Binvert(aluopconv_1_binvert),
    .CarryIn(alu1_4_carryout), .O1(aluopconv_1_o1), .O2(aluopconv_1_o2), .CarryOut(alu1_5_carryout),
    .Result(alu1_5_result));  // open: Less
  ALU1 alu1_6 (
    .A(bitconv1_1_b5), .B(bitconv1_2_b5), .Ainvert(aluopconv_1_ainvert), .Binvert(aluopconv_1_binvert),
    .CarryIn(alu1_5_carryout), .O1(aluopconv_1_o1), .O2(aluopconv_1_o2), .CarryOut(alu1_6_carryout),
    .Result(alu1_6_result));  // open: Less
  ALU1 alu1_7 (
    .A(bitconv1_1_b6), .B(bitconv1_2_b6), .Ainvert(aluopconv_1_ainvert), .Binvert(aluopconv_1_binvert),
    .CarryIn(alu1_6_carryout), .O1(aluopconv_1_o1), .O2(aluopconv_1_o2), .CarryOut(alu1_7_carryout),
    .Result(alu1_7_result));  // open: Less
  ALU1 alu1_8 (
    .A(bitconv1_1_b7), .B(bitconv1_2_b7), .Ainvert(aluopconv_1_ainvert), .Binvert(aluopconv_1_binvert),
    .CarryIn(alu1_7_carryout), .O1(aluopconv_1_o1), .O2(aluopconv_1_o2), .CarryOut(alu1_8_carryout),
    .Result(alu1_8_result));  // open: Less
  ALU1 alu1_9 (
    .A(bitconv1_1_b8), .B(bitconv1_2_b8), .Ainvert(aluopconv_1_ainvert), .Binvert(aluopconv_1_binvert),
    .CarryIn(alu1_8_carryout), .O1(aluopconv_1_o1), .O2(aluopconv_1_o2), .CarryOut(alu1_9_carryout),
    .Result(alu1_9_result));  // open: Less
  ALU1 alu1_10 (
    .A(bitconv1_1_b9), .B(bitconv1_2_b9), .Ainvert(aluopconv_1_ainvert), .Binvert(aluopconv_1_binvert),
    .CarryIn(alu1_9_carryout), .O1(aluopconv_1_o1), .O2(aluopconv_1_o2), .CarryOut(alu1_10_carryout),
    .Result(alu1_10_result));  // open: Less
  ALU1 alu1_11 (
    .A(bitconv1_1_b10), .B(bitconv1_2_b10), .Ainvert(aluopconv_1_ainvert), .Binvert(aluopconv_1_binvert),
    .CarryIn(alu1_10_carryout), .O1(aluopconv_1_o1), .O2(aluopconv_1_o2), .CarryOut(alu1_11_carryout),
    .Result(alu1_11_result));  // open: Less
  ALU1 alu1_12 (
    .A(bitconv1_1_b11), .B(bitconv1_2_b11), .Ainvert(aluopconv_1_ainvert), .Binvert(aluopconv_1_binvert),
    .CarryIn(alu1_11_carryout), .O1(aluopconv_1_o1), .O2(aluopconv_1_o2), .CarryOut(alu1_12_carryout),
    .Result(alu1_12_result));  // open: Less
  ALU1 alu1_13 (
    .A(bitconv1_1_b12), .B(bitconv1_2_b12), .Ainvert(aluopconv_1_ainvert), .Binvert(aluopconv_1_binvert),
    .CarryIn(alu1_12_carryout), .O1(aluopconv_1_o1), .O2(aluopconv_1_o2), .CarryOut(alu1_13_carryout),
    .Result(alu1_13_result));  // open: Less
  ALU1 alu1_14 (
    .A(bitconv1_1_b13), .B(bitconv1_2_b13), .Ainvert(aluopconv_1_ainvert), .Binvert(aluopconv_1_binvert),
    .CarryIn(alu1_13_carryout), .O1(aluopconv_1_o1), .O2(aluopconv_1_o2), .CarryOut(alu1_14_carryout),
    .Result(alu1_14_result));  // open: Less
  ALU1 alu1_15 (
    .A(bitconv1_1_b14), .B(bitconv1_2_b14), .Ainvert(aluopconv_1_ainvert), .Binvert(aluopconv_1_binvert),
    .CarryIn(alu1_14_carryout), .O1(aluopconv_1_o1), .O2(aluopconv_1_o2), .CarryOut(alu1_15_carryout),
    .Result(alu1_15_result));  // open: Less
  ALU1 alu1_16 (
    .A(bitconv1_1_b15), .B(bitconv1_2_b15), .Ainvert(aluopconv_1_ainvert), .Binvert(aluopconv_1_binvert),
    .CarryIn(alu1_15_carryout), .O1(aluopconv_1_o1), .O2(aluopconv_1_o2), .CarryOut(alu1_16_carryout),
    .Result(alu1_16_result));  // open: Less
  ALU1 alu1_17 (
    .A(bitconv1_1_b16), .B(bitconv1_2_b16), .Ainvert(aluopconv_1_ainvert), .Binvert(aluopconv_1_binvert),
    .CarryIn(alu1_16_carryout), .O1(aluopconv_1_o1), .O2(aluopconv_1_o2), .CarryOut(alu1_17_carryout),
    .Result(alu1_17_result));  // open: Less
  ALU1 alu1_18 (
    .A(bitconv1_1_b17), .B(bitconv1_2_b17), .Ainvert(aluopconv_1_ainvert), .Binvert(aluopconv_1_binvert),
    .CarryIn(alu1_17_carryout), .O1(aluopconv_1_o1), .O2(aluopconv_1_o2), .CarryOut(alu1_18_carryout),
    .Result(alu1_18_result));  // open: Less
  ALU1 alu1_19 (
    .A(bitconv1_1_b18), .B(bitconv1_2_b18), .Ainvert(aluopconv_1_ainvert), .Binvert(aluopconv_1_binvert),
    .CarryIn(alu1_18_carryout), .O1(aluopconv_1_o1), .O2(aluopconv_1_o2), .CarryOut(alu1_19_carryout),
    .Result(alu1_19_result));  // open: Less
  ALU1 alu1_20 (
    .A(bitconv1_1_b19), .B(bitconv1_2_b19), .Ainvert(aluopconv_1_ainvert), .Binvert(aluopconv_1_binvert),
    .CarryIn(alu1_19_carryout), .O1(aluopconv_1_o1), .O2(aluopconv_1_o2), .CarryOut(alu1_20_carryout),
    .Result(alu1_20_result));  // open: Less
  ALU1 alu1_21 (
    .A(bitconv1_1_b20), .B(bitconv1_2_b20), .Ainvert(aluopconv_1_ainvert), .Binvert(aluopconv_1_binvert),
    .CarryIn(alu1_20_carryout), .O1(aluopconv_1_o1), .O2(aluopconv_1_o2), .CarryOut(alu1_21_carryout),
    .Result(alu1_21_result));  // open: Less
  ALU1 alu1_22 (
    .A(bitconv1_1_b21), .B(bitconv1_2_b21), .Ainvert(aluopconv_1_ainvert), .Binvert(aluopconv_1_binvert),
    .CarryIn(alu1_21_carryout), .O1(aluopconv_1_o1), .O2(aluopconv_1_o2), .CarryOut(alu1_22_carryout),
    .Result(alu1_22_result));  // open: Less
  ALU1 alu1_23 (
    .A(bitconv1_1_b22), .B(bitconv1_2_b22), .Ainvert(aluopconv_1_ainvert), .Binvert(aluopconv_1_binvert),
    .CarryIn(alu1_22_carryout), .O1(aluopconv_1_o1), .O2(aluopconv_1_o2), .CarryOut(alu1_23_carryout),
    .Result(alu1_23_result));  // open: Less
  ALU1 alu1_24 (
    .A(bitconv1_1_b23), .B(bitconv1_2_b23), .Ainvert(aluopconv_1_ainvert), .Binvert(aluopconv_1_binvert),
    .CarryIn(alu1_23_carryout), .O1(aluopconv_1_o1), .O2(aluopconv_1_o2), .CarryOut(alu1_24_carryout),
    .Result(alu1_24_result));  // open: Less
  ALU1 alu1_25 (
    .A(bitconv1_1_b24), .B(bitconv1_2_b24), .Ainvert(aluopconv_1_ainvert), .Binvert(aluopconv_1_binvert),
    .CarryIn(alu1_24_carryout), .O1(aluopconv_1_o1), .O2(aluopconv_1_o2), .CarryOut(alu1_25_carryout),
    .Result(alu1_25_result));  // open: Less
  ALU1 alu1_26 (
    .A(bitconv1_1_b25), .B(bitconv1_2_b25), .Ainvert(aluopconv_1_ainvert), .Binvert(aluopconv_1_binvert),
    .CarryIn(alu1_25_carryout), .O1(aluopconv_1_o1), .O2(aluopconv_1_o2), .CarryOut(alu1_26_carryout),
    .Result(alu1_26_result));  // open: Less
  ALU1 alu1_27 (
    .A(bitconv1_1_b26), .B(bitconv1_2_b26), .Ainvert(aluopconv_1_ainvert), .Binvert(aluopconv_1_binvert),
    .CarryIn(alu1_26_carryout), .O1(aluopconv_1_o1), .O2(aluopconv_1_o2), .CarryOut(alu1_27_carryout),
    .Result(alu1_27_result));  // open: Less
  ALU1 alu1_28 (
    .A(bitconv1_1_b27), .B(bitconv1_2_b27), .Ainvert(aluopconv_1_ainvert), .Binvert(aluopconv_1_binvert),
    .CarryIn(alu1_27_carryout), .O1(aluopconv_1_o1), .O2(aluopconv_1_o2), .CarryOut(alu1_28_carryout),
    .Result(alu1_28_result));  // open: Less
  ALU1 alu1_29 (
    .A(bitconv1_1_b28), .B(bitconv1_2_b28), .Ainvert(aluopconv_1_ainvert), .Binvert(aluopconv_1_binvert),
    .CarryIn(alu1_28_carryout), .O1(aluopconv_1_o1), .O2(aluopconv_1_o2), .CarryOut(alu1_29_carryout),
    .Result(alu1_29_result));  // open: Less
  ALU1 alu1_30 (
    .A(bitconv1_1_b29), .B(bitconv1_2_b29), .Ainvert(aluopconv_1_ainvert), .Binvert(aluopconv_1_binvert),
    .CarryIn(alu1_29_carryout), .O1(aluopconv_1_o1), .O2(aluopconv_1_o2), .CarryOut(alu1_30_carryout),
    .Result(alu1_30_result));  // open: Less
  ALU1 alu1_31 (
    .A(bitconv1_1_b30), .B(bitconv1_2_b30), .Ainvert(aluopconv_1_ainvert), .Binvert(aluopconv_1_binvert),
    .CarryIn(alu1_30_carryout), .O1(aluopconv_1_o1), .O2(aluopconv_1_o2), .CarryOut(alu1_31_carryout),
    .Result(alu1_31_result));  // open: Less
  ALU1 alu1_32 (
    .A(bitconv1_1_b31), .B(bitconv1_2_b31), .Ainvert(aluopconv_1_ainvert), .Binvert(aluopconv_1_binvert),
    .CarryIn(alu1_31_carryout), .O1(aluopconv_1_o1), .O2(aluopconv_1_o2), .CarryOut(Overflow),
    .Result(alu1_32_result));  // open: Less
  or or_1 (or_1_out, alu1_1_result, alu1_2_result, alu1_3_result, alu1_4_result, alu1_5_result, alu1_6_result, alu1_7_result, alu1_8_result, alu1_9_result, alu1_10_result, alu1_11_result, alu1_12_result, alu1_13_result, alu1_14_result, alu1_15_result, alu1_16_result, alu1_17_result, alu1_18_result, alu1_19_result, alu1_20_result, alu1_21_result, alu1_22_result, alu1_23_result, alu1_24_result, alu1_25_result, alu1_26_result, alu1_27_result, alu1_28_result, alu1_29_result, alu1_30_result, alu1_31_result, alu1_32_result);
  not not_1 (Zero, or_1_out);
  BitConv32 bitconv32_1 (
    .B2(alu1_3_result), .B3(alu1_4_result), .B4(alu1_5_result), .B5(alu1_6_result), .B6(alu1_7_result),
    .B7(alu1_8_result), .B8(alu1_9_result), .B9(alu1_10_result), .B10(alu1_11_result), .B11(alu1_12_result),
    .B12(alu1_13_result), .B13(alu1_14_result), .B14(alu1_15_result), .B0(alu1_1_result),
    .B15(alu1_16_result), .B16(alu1_17_result), .B17(alu1_18_result), .B18(alu1_19_result),
    .B19(alu1_20_result), .B20(alu1_21_result), .B21(alu1_22_result), .B22(alu1_23_result),
    .B23(alu1_24_result), .B24(alu1_25_result), .B1(alu1_2_result), .B25(alu1_26_result),
    .B26(alu1_27_result), .B27(alu1_28_result), .B28(alu1_29_result), .B29(alu1_30_result),
    .B30(alu1_31_result), .B31(alu1_32_result), .Bit32(Result));
endmodule

module BitConv32 (
  input  B0,
  input  B1,
  input  B2,
  input  B3,
  input  B4,
  input  B5,
  input  B6,
  input  B7,
  input  B8,
  input  B9,
  input  B10,
  input  B11,
  input  B12,
  input  B13,
  input  B14,
  input  B15,
  input  B16,
  input  B17,
  input  B18,
  input  B19,
  input  B20,
  input  B21,
  input  B22,
  input  B23,
  input  B24,
  input  B25,
  input  B26,
  input  B27,
  input  B28,
  input  B29,
  input  B30,
  input  B31,
  output [31:0] Bit32
);


  assign Bit32 = {B31, B30, B29, B28, B27, B26, B25, B24, B23, B22, B21, B20, B19, B18, B17, B16, B15, B14, B13, B12, B11, B10, B9, B8, B7, B6, B5, B4, B3, B2, B1, B0};
endmodule

module BitConv1 (
  input  [31:0] Bit32,
  output B0,
  output B1,
  output B2,
  output B3,
  output B4,
  output B5,
  output B6,
  output B7,
  output B8,
  output B9,
  output B10,
  output B11,
  output B12,
  output B13,
  output B14,
  output B15,
  output B16,
  output B17,
  output B18,
  output B19,
  output B20,
  output B21,
  output B22,
  output B23,
  output B24,
  output B25,
  output B26,
  output B27,
  output B28,
  output B29,
  output B30,
  output B31
);


  assign B0 = Bit32[0];
  assign B1 = Bit32[1];
  assign B2 = Bit32[2];
  assign B3 = Bit32[3];
  assign B4 = Bit32[4];
  assign B5 = Bit32[5];
  assign B6 = Bit32[6];
  assign B7 = Bit32[7];
  assign B8 = Bit32[8];
  assign B9 = Bit32[9];
  assign B10 = Bit32[10];
  assign B11 = Bit32[11];
  assign B12 = Bit32[12];
  assign B13 = Bit32[13];
  assign B14 = Bit32[14];
  assign B15 = Bit32[15];
  assign B16 = Bit32[16];
  assign B17 = Bit32[17];
  assign B18 = Bit32[18];
  assign B19 = Bit32[19];
  assign B20 = Bit32[20];
  assign B21 = Bit32[21];
  assign B22 = Bit32[22];
  assign B23 = Bit32[23];
  assign B24 = Bit32[24];
  assign B25 = Bit32[25];
  assign B26 = Bit32[26];
  assign B27 = Bit32[27];
  assign B28 = Bit32[28];
  assign B29 = Bit32[29];
  assign B30 = Bit32[30];
  assign B31 = Bit32[31];
endmodule

module DLatch (
  input  C,
  input  D,
  output Q
);

  wire and_1_out, and_2_out, nor_2_out, not_1_out;

  not not_1 (not_1_out, D);
  and and_1 (and_1_out, C, not_1_out);
  nor nor_1 (Q, and_1_out, nor_2_out);
  nor nor_2 (nor_2_out, Q, and_2_out);
  and and_2 (and_2_out, C, D);
endmodule

module ALUopConv (
  input  [3:0] ALUop,
  output Ainvert,
  output O2,
  output Binvert,
  output O1
);


  assign Ainvert = ALUop[3];
  assign Binvert = ALUop[2];
  assign O1 = ALUop[1];
  assign O2 = ALUop[0];
endmodule

module Control (
  input  [5:0] OpCode,
  output RegDst,
  output ALUSrc,
  output MemToReg,
  output RegWrite,
  output MemRead,
  output MemWrite,
  output Branch,
  output Op1,
  output Op0
);

  wire and_1_out, and_2_out, and_3_out, and_4_out, and_5_out, and_6_out, and_7_out, and_8_out, and_9_out,
       and_10_out, and_11_out, and_12_out, and_13_out, and_14_out, and_15_out, and_16_out, not_1_out,
       not_2_out, not_3_out, not_4_out, not_5_out, not_6_out, not_7_out, not_8_out, not_9_out, not_10_out,
       not_11_out, not_12_out, not_13_out, not_14_out, not_15_out, not_16_out;

  not not_1 (not_1_out, OpCode[0]);
  not not_2 (not_2_out, OpCode[1]);
  not not_3 (not_3_out, OpCode[2]);
  not not_4 (not_4_out, OpCode[3]);
  not not_5 (not_5_out, OpCode[4]);
  not not_6 (not_6_out, OpCode[5]);
  not not_7 (not_7_out, OpCode[2]);
  not not_8 (not_8_out, OpCode[3]);
  not not_9 (not_9_out, OpCode[4]);
  not not_10 (not_10_out, OpCode[2]);
  not not_11 (not_11_out, OpCode[4]);
  not not_12 (not_12_out, OpCode[0]);
  not not_13 (not_13_out, OpCode[1]);
  not not_14 (not_14_out, OpCode[3]);
  not not_15 (not_15_out, OpCode[4]);
  not not_16 (not_16_out, OpCode[5]);
  and and_1 (and_1_out, not_1_out, not_2_out);
  and and_2 (and_2_out, not_3_out, not_4_out);
  and and_3 (and_3_out, not_5_out, not_6_out);
  and and_4 (and_4_out, OpCode[0], OpCode[1]);
  and and_5 (and_5_out, not_7_out, not_8_out);
  and and_6 (and_6_out, not_9_out, OpCode[5]);
  and and_7 (and_7_out, OpCode[0], OpCode[1]);
  and and_8 (and_8_out, not_10_out, OpCode[3]);
  and and_9 (and_9_out, not_11_out, OpCode[5]);
  and and_10 (and_10_out, not_12_out, not_13_out);
  and and_11 (and_11_out, OpCode[2], not_14_out);
  and and_12 (and_12_out, not_15_out, not_16_out);
  and and_13 (and_13_out, and_1_out, and_2_out);
  and and_14 (and_14_out, and_4_out, and_5_out);
  and and_15 (and_15_out, and_7_out, and_8_out);
  and and_16 (and_16_out, and_10_out, and_11_out);
  and and_17 (Op1, and_13_out, and_3_out);
  and and_18 (MemRead, and_14_out, and_6_out);
  and and_19 (MemWrite, and_15_out, and_9_out);
  and and_20 (Branch, and_16_out, and_12_out);
  or or_1 (ALUSrc, MemWrite, MemRead);
  or or_2 (RegWrite, Op1, MemRead);

  assign MemToReg = MemRead;
  assign Op0 = Branch;
  assign RegDst = Op1;
endmodule

module ALUControl (
  input  Op0,
  input  Op1,
  input  [5:0] Funct,
  output [3:0] Operation
);

  wire and_1_out, and_2_out, and_3_out, and_4_out, and_5_out, and_6_out, and_7_out, and_8_out, and_9_out,
       and_10_out, and_11_out, and_12_out, and_13_out, and_14_out, and_15_out, and_16_out, and_17_out,
       and_18_out, and_19_out, and_20_out, and_21_out, and_22_out, and_23_out, and_24_out, and_25_out,
       and_26_out, and_27_out, and_28_out, and_29_out, and_30_out, and_32_out, and_33_out, and_34_out,
       not_1_out, not_2_out, not_3_out, not_4_out, not_5_out, not_6_out, not_7_out, not_8_out, not_9_out,
       not_10_out, not_11_out, not_12_out, not_13_out, not_14_out, not_15_out, not_16_out, not_17_out,
       not_18_out, not_19_out, not_20_out, not_21_out, not_22_out, not_23_out;

  not not_1 (not_1_out, Op0);
  not not_2 (not_2_out, Op1);
  not not_3 (not_3_out, Op1);
  not not_4 (not_4_out, Op0);
  not not_5 (not_5_out, Funct[0]);
  not not_6 (not_6_out, Funct[1]);
  not not_7 (not_7_out, Funct[2]);
  not not_8 (not_8_out, Funct[3]);
  not not_9 (not_9_out, Funct[4]);
  not not_10 (not_10_out, Funct[0]);
  not not_11 (not_11_out, Funct[2]);
  not not_12 (not_12_out, Funct[3]);
  not not_13 (not_13_out, Funct[4]);
  not not_14 (not_14_out, Funct[0]);
  not not_15 (not_15_out, Funct[1]);
  not not_16 (not_16_out, Funct[3]);
  not not_17 (not_17_out, Funct[4]);
  not not_18 (not_18_out, Funct[1]);
  not not_19 (not_19_out, Funct[3]);
  not not_20 (not_20_out, Funct[4]);
  not not_21 (not_21_out, Funct[0]);
  not not_22 (not_22_out, Funct[2]);
  not not_23 (not_23_out, Funct[4]);
  and and_1 (and_1_out, not_1_out, not_2_out);
  and and_2 (and_2_out, Op0, not_3_out);
  and and_3 (and_3_out, not_4_out, Op1);
  and and_4 (and_4_out, not_5_out, not_6_out);
  and and_5 (and_5_out, not_7_out, not_8_out);
  and and_6 (and_6_out, not_9_out, Funct[5]);
  and and_7 (and_7_out, not_10_out, Funct[1]);
  and and_8 (and_8_out, not_11_out, not_12_out);
  and and_9 (and_9_out, not_13_out, Funct[5]);
  and and_10 (and_10_out, not_14_out, not_15_out);
  and and_11 (and_11_out, Funct[2], not_16_out);
  and and_12 (and_12_out, not_17_out, Funct[5]);
  and and_13 (and_13_out, Funct[0], not_18_out);
  and and_14 (and_14_out, Funct[2], not_19_out);
  and and_15 (and_15_out, not_20_out, Funct[5]);
  and and_16 (and_16_out, not_21_out, Funct[1]);
  and and_17 (and_17_out, not_22_out, Funct[3]);
  and and_18 (and_18_out, not_23_out, Funct[5]);
  and and_19 (and_19_out, and_5_out, and_6_out);
  and and_20 (and_20_out, and_8_out, and_9_out);
  and and_21 (and_21_out, and_11_out, and_12_out);
  and and_22 (and_22_out, and_14_out, and_15_out);
  and and_23 (and_23_out, and_17_out, and_18_out);
  and and_24 (and_24_out, and_4_out, and_19_out);
  and and_25 (and_25_out, and_7_out, and_20_out);
  and and_26 (and_26_out, and_10_out, and_21_out);
  and and_27 (and_27_out, and_13_out, and_22_out);
  and and_28 (and_28_out, and_16_out, and_23_out);
  and and_29 (and_29_out, and_3_out, and_24_out);
  and and_30 (and_30_out, and_3_out, and_25_out);
  and and_31 (Operation[3], 1'b0, and_32_out);
  and and_32 (and_32_out, and_3_out, and_26_out);
  and and_33 (and_33_out, and_3_out, and_27_out);
  and and_34 (and_34_out, and_3_out, and_28_out);
  or or_1 (Operation[0], and_34_out, and_33_out, Operation[3]);
  or or_2 (Operation[1], and_34_out, and_1_out, and_29_out, and_30_out, and_2_out, Operation[3]);
  or or_3 (Operation[2], and_30_out, Operation[3], and_34_out, and_2_out);
endmodule

module Register32 (
  input  Clock,
  input  [31:0] DataIn,
  output [31:0] DataOut
);

  DLatch dlatch_1 (.D(DataIn[0]), .C(Clock), .Q(DataOut[0]));
  DLatch dlatch_2 (.D(DataIn[1]), .C(Clock), .Q(DataOut[1]));
  DLatch dlatch_3 (.D(DataIn[2]), .C(Clock), .Q(DataOut[2]));
  DLatch dlatch_4 (.D(DataIn[3]), .C(Clock), .Q(DataOut[3]));
  DLatch dlatch_5 (.D(DataIn[4]), .C(Clock), .Q(DataOut[4]));
  DLatch dlatch_6 (.D(DataIn[5]), .C(Clock), .Q(DataOut[5]));
  DLatch dlatch_7 (.D(DataIn[6]), .C(Clock), .Q(DataOut[6]));
  DLatch dlatch_8 (.D(DataIn[7]), .C(Clock), .Q(DataOut[7]));
  DLatch dlatch_9 (.D(DataIn[8]), .C(Clock), .Q(DataOut[8]));
  DLatch dlatch_10 (.D(DataIn[9]), .C(Clock), .Q(DataOut[9]));
  DLatch dlatch_11 (.D(DataIn[10]), .C(Clock), .Q(DataOut[10]));
  DLatch dlatch_12 (.D(DataIn[11]), .C(Clock), .Q(DataOut[11]));
  DLatch dlatch_13 (.D(DataIn[12]), .C(Clock), .Q(DataOut[12]));
  DLatch dlatch_14 (.D(DataIn[13]), .C(Clock), .Q(DataOut[13]));
  DLatch dlatch_15 (.D(DataIn[14]), .C(Clock), .Q(DataOut[14]));
  DLatch dlatch_16 (.D(DataIn[15]), .C(Clock), .Q(DataOut[15]));
  DLatch dlatch_17 (.D(DataIn[16]), .C(Clock), .Q(DataOut[16]));
  DLatch dlatch_18 (.D(DataIn[17]), .C(Clock), .Q(DataOut[17]));
  DLatch dlatch_19 (.D(DataIn[18]), .C(Clock), .Q(DataOut[18]));
  DLatch dlatch_20 (.D(DataIn[19]), .C(Clock), .Q(DataOut[19]));
  DLatch dlatch_21 (.D(DataIn[20]), .C(Clock), .Q(DataOut[20]));
  DLatch dlatch_22 (.D(DataIn[21]), .C(Clock), .Q(DataOut[21]));
  DLatch dlatch_23 (.D(DataIn[22]), .C(Clock), .Q(DataOut[22]));
  DLatch dlatch_24 (.D(DataIn[23]), .C(Clock), .Q(DataOut[23]));
  DLatch dlatch_25 (.D(DataIn[24]), .C(Clock), .Q(DataOut[24]));
  DLatch dlatch_26 (.D(DataIn[25]), .C(Clock), .Q(DataOut[25]));
  DLatch dlatch_27 (.D(DataIn[26]), .C(Clock), .Q(DataOut[26]));
  DLatch dlatch_28 (.D(DataIn[27]), .C(Clock), .Q(DataOut[27]));
  DLatch dlatch_29 (.D(DataIn[28]), .C(Clock), .Q(DataOut[28]));
  DLatch dlatch_30 (.D(DataIn[29]), .C(Clock), .Q(DataOut[29]));
  DLatch dlatch_31 (.D(DataIn[30]), .C(Clock), .Q(DataOut[30]));
  DLatch dlatch_32 (.D(DataIn[31]), .C(Clock), .Q(DataOut[31]));
endmodule

module RegistersBlock (
  input  [31:0] WriteData,
  input  Clock,
  input  [4:0] ReadReg1,
  input  [4:0] ReadReg2,
  input  [4:0] WriteReg,
  output [31:0] ReadData1,
  output [31:0] ReadData2
);

  wire and_1_out, and_2_out, and_3_out, and_4_out, and_5_out, and_6_out, and_7_out, and_8_out, and_9_out,
       and_10_out, and_11_out, and_12_out, and_13_out, and_14_out, and_15_out, and_16_out, and_17_out,
       and_18_out, and_19_out, and_20_out, and_21_out, and_22_out, and_23_out, and_24_out, and_25_out,
       and_26_out, and_27_out, and_28_out, and_29_out, and_30_out, and_31_out, and_32_out,
       registerdecoder_1_reg0, registerdecoder_1_reg1, registerdecoder_1_reg2, registerdecoder_1_reg3,
       registerdecoder_1_reg4, registerdecoder_1_reg5, registerdecoder_1_reg6, registerdecoder_1_reg7,
       registerdecoder_1_reg8, registerdecoder_1_reg9, registerdecoder_1_reg10, registerdecoder_1_reg11,
       registerdecoder_1_reg12, registerdecoder_1_reg13, registerdecoder_1_reg14, registerdecoder_1_reg15,
       registerdecoder_1_reg16, registerdecoder_1_reg17, registerdecoder_1_reg18, registerdecoder_1_reg19,
       registerdecoder_1_reg20, registerdecoder_1_reg21, registerdecoder_1_reg22, registerdecoder_1_reg23,
       registerdecoder_1_reg24, registerdecoder_1_reg25, registerdecoder_1_reg26, registerdecoder_1_reg27,
       registerdecoder_1_reg28, registerdecoder_1_reg29, registerdecoder_1_reg30, registerdecoder_1_reg31;
  wire [31:0] register32_1_dataout, register32_2_dataout, register32_3_dataout, register32_4_dataout,
       register32_5_dataout, register32_6_dataout, register32_7_dataout, register32_8_dataout,
       register32_9_dataout, register32_10_dataout, register32_11_dataout, register32_12_dataout,
       register32_13_dataout, register32_14_dataout, register32_15_dataout, register32_16_dataout,
       register32_17_dataout, register32_18_dataout, register32_19_dataout, register32_20_dataout,
       register32_21_dataout, register32_22_dataout, register32_23_dataout, register32_24_dataout,
       register32_25_dataout, register32_26_dataout, register32_27_dataout, register32_28_dataout,
       register32_29_dataout, register32_30_dataout, register32_31_dataout, register32_32_dataout;

  RegisterDecoder registerdecoder_1 (
    .RegAddr(WriteReg), .Reg4(registerdecoder_1_reg4), .Reg5(registerdecoder_1_reg5),
    .Reg6(registerdecoder_1_reg6), .Reg7(registerdecoder_1_reg7), .Reg8(registerdecoder_1_reg8),
    .Reg9(registerdecoder_1_reg9), .Reg10(registerdecoder_1_reg10), .Reg11(registerdecoder_1_reg11),
    .Reg12(registerdecoder_1_reg12), .Reg13(registerdecoder_1_reg13), .Reg14(registerdecoder_1_reg14),
    .Reg15(registerdecoder_1_reg15), .Reg0(registerdecoder_1_reg0), .Reg16(registerdecoder_1_reg16),
    .Reg17(registerdecoder_1_reg17), .Reg18(registerdecoder_1_reg18), .Reg19(registerdecoder_1_reg19),
    .Reg20(registerdecoder_1_reg20), .Reg21(registerdecoder_1_reg21), .Reg22(registerdecoder_1_reg22),
    .Reg23(registerdecoder_1_reg23), .Reg24(registerdecoder_1_reg24), .Reg25(registerdecoder_1_reg25),
    .Reg1(registerdecoder_1_reg1), .Reg26(registerdecoder_1_reg26), .Reg27(registerdecoder_1_reg27),
    .Reg28(registerdecoder_1_reg28), .Reg29(registerdecoder_1_reg29), .Reg30(registerdecoder_1_reg30),
    .Reg31(registerdecoder_1_reg31), .Reg2(registerdecoder_1_reg2), .Reg3(registerdecoder_1_reg3));
  and and_1 (and_1_out, Clock, registerdecoder_1_reg0);
  and and_2 (and_2_out, Clock, registerdecoder_1_reg1);
  and and_3 (and_3_out, Clock, registerdecoder_1_reg2);
  and and_4 (and_4_out, Clock, registerdecoder_1_reg3);
  and and_5 (and_5_out, Clock, registerdecoder_1_reg4);
  and and_6 (and_6_out, Clock, registerdecoder_1_reg5);
  and and_7 (and_7_out, Clock, registerdecoder_1_reg6);
  and and_8 (and_8_out, Clock, registerdecoder_1_reg7);
  and and_9 (and_9_out, Clock, registerdecoder_1_reg8);
  and and_10 (and_10_out, Clock, registerdecoder_1_reg9);
  and and_11 (and_11_out, Clock, registerdecoder_1_reg10);
  and and_12 (and_12_out, Clock, registerdecoder_1_reg11);
  and and_13 (and_13_out, Clock, registerdecoder_1_reg12);
  and and_14 (and_14_out, Clock, registerdecoder_1_reg13);
  and and_15 (and_15_out, Clock, registerdecoder_1_reg14);
  and and_16 (and_16_out, Clock, registerdecoder_1_reg15);
  and and_17 (and_17_out, Clock, registerdecoder_1_reg16);
  and and_18 (and_18_out, Clock, registerdecoder_1_reg17);
  and and_19 (and_19_out, Clock, registerdecoder_1_reg18);
  and and_20 (and_20_out, Clock, registerdecoder_1_reg19);
  and and_21 (and_21_out, Clock, registerdecoder_1_reg20);
  and and_22 (and_22_out, Clock, registerdecoder_1_reg21);
  and and_23 (and_23_out, Clock, registerdecoder_1_reg22);
  and and_24 (and_24_out, Clock, registerdecoder_1_reg23);
  and and_25 (and_25_out, Clock, registerdecoder_1_reg24);
  and and_26 (and_26_out, Clock, registerdecoder_1_reg25);
  and and_27 (and_27_out, Clock, registerdecoder_1_reg26);
  and and_28 (and_28_out, Clock, registerdecoder_1_reg27);
  and and_29 (and_29_out, Clock, registerdecoder_1_reg28);
  and and_30 (and_30_out, Clock, registerdecoder_1_reg29);
  and and_31 (and_31_out, Clock, registerdecoder_1_reg30);
  and and_32 (and_32_out, Clock, registerdecoder_1_reg31);
  Register32 register32_1 (.DataIn(WriteData), .Clock(and_1_out), .DataOut(register32_1_dataout));
  Register32 register32_2 (.DataIn(WriteData), .Clock(and_2_out), .DataOut(register32_2_dataout));
  Register32 register32_3 (.DataIn(WriteData), .Clock(and_3_out), .DataOut(register32_3_dataout));
  Register32 register32_4 (.DataIn(WriteData), .Clock(and_4_out), .DataOut(register32_4_dataout));
  Register32 register32_5 (.DataIn(WriteData), .Clock(and_5_out), .DataOut(register32_5_dataout));
  Register32 register32_6 (.DataIn(WriteData), .Clock(and_6_out), .DataOut(register32_6_dataout));
  Register32 register32_7 (.DataIn(WriteData), .Clock(and_7_out), .DataOut(register32_7_dataout));
  Register32 register32_8 (.DataIn(WriteData), .Clock(and_8_out), .DataOut(register32_8_dataout));
  Register32 register32_9 (.DataIn(WriteData), .Clock(and_9_out), .DataOut(register32_9_dataout));
  Register32 register32_10 (.DataIn(WriteData), .Clock(and_10_out), .DataOut(register32_10_dataout));
  Register32 register32_11 (.DataIn(WriteData), .Clock(and_11_out), .DataOut(register32_11_dataout));
  Register32 register32_12 (.DataIn(WriteData), .Clock(and_12_out), .DataOut(register32_12_dataout));
  Register32 register32_13 (.DataIn(WriteData), .Clock(and_13_out), .DataOut(register32_13_dataout));
  Register32 register32_14 (.DataIn(WriteData), .Clock(and_14_out), .DataOut(register32_14_dataout));
  Register32 register32_15 (.DataIn(WriteData), .Clock(and_15_out), .DataOut(register32_15_dataout));
  Register32 register32_16 (.DataIn(WriteData), .Clock(and_16_out), .DataOut(register32_16_dataout));
  Register32 register32_17 (.DataIn(WriteData), .Clock(and_17_out), .DataOut(register32_17_dataout));
  Register32 register32_18 (.DataIn(WriteData), .Clock(and_18_out), .DataOut(register32_18_dataout));
  Register32 register32_19 (.DataIn(WriteData), .Clock(and_19_out), .DataOut(register32_19_dataout));
  Register32 register32_20 (.DataIn(WriteData), .Clock(and_20_out), .DataOut(register32_20_dataout));
  Register32 register32_21 (.DataIn(WriteData), .Clock(and_21_out), .DataOut(register32_21_dataout));
  Register32 register32_22 (.DataIn(WriteData), .Clock(and_22_out), .DataOut(register32_22_dataout));
  Register32 register32_23 (.DataIn(WriteData), .Clock(and_23_out), .DataOut(register32_23_dataout));
  Register32 register32_24 (.DataIn(WriteData), .Clock(and_24_out), .DataOut(register32_24_dataout));
  Register32 register32_25 (.DataIn(WriteData), .Clock(and_25_out), .DataOut(register32_25_dataout));
  Register32 register32_26 (.DataIn(WriteData), .Clock(and_26_out), .DataOut(register32_26_dataout));
  Register32 register32_27 (.DataIn(WriteData), .Clock(and_27_out), .DataOut(register32_27_dataout));
  Register32 register32_28 (.DataIn(WriteData), .Clock(and_28_out), .DataOut(register32_28_dataout));
  Register32 register32_29 (.DataIn(WriteData), .Clock(and_29_out), .DataOut(register32_29_dataout));
  Register32 register32_30 (.DataIn(WriteData), .Clock(and_30_out), .DataOut(register32_30_dataout));
  Register32 register32_31 (.DataIn(WriteData), .Clock(and_31_out), .DataOut(register32_31_dataout));
  Register32 register32_32 (.DataIn(WriteData), .Clock(and_32_out), .DataOut(register32_32_dataout));
  RegisterMux registermux_1 (
    .RegAddr(ReadReg1), .Reg5(register32_6_dataout), .Reg6(register32_7_dataout),
    .Reg7(register32_8_dataout), .Reg8(register32_9_dataout), .Reg9(register32_10_dataout),
    .Reg10(register32_11_dataout), .Reg0(register32_1_dataout), .Reg11(register32_12_dataout),
    .Reg12(register32_13_dataout), .Reg13(register32_14_dataout), .Reg14(register32_15_dataout),
    .Reg15(register32_16_dataout), .Reg16(register32_17_dataout), .Reg17(register32_18_dataout),
    .Reg18(register32_19_dataout), .Reg19(register32_20_dataout), .Reg20(register32_21_dataout),
    .Reg1(register32_2_dataout), .Reg21(register32_22_dataout), .Reg22(register32_23_dataout),
    .Reg23(register32_24_dataout), .Reg24(register32_25_dataout), .Reg25(register32_26_dataout),
    .Reg26(register32_27_dataout), .Reg27(register32_28_dataout), .Reg28(register32_29_dataout),
    .Reg29(register32_30_dataout), .Reg30(register32_31_dataout), .Reg2(register32_3_dataout),
    .Reg31(register32_32_dataout), .Reg3(register32_4_dataout), .Reg4(register32_5_dataout),
    .DataOut(ReadData1));
  RegisterMux registermux_2 (
    .RegAddr(ReadReg2), .Reg5(register32_6_dataout), .Reg6(register32_7_dataout),
    .Reg7(register32_8_dataout), .Reg8(register32_9_dataout), .Reg9(register32_10_dataout),
    .Reg10(register32_11_dataout), .Reg0(register32_1_dataout), .Reg11(register32_12_dataout),
    .Reg12(register32_13_dataout), .Reg13(register32_14_dataout), .Reg14(register32_15_dataout),
    .Reg15(register32_16_dataout), .Reg16(register32_17_dataout), .Reg17(register32_18_dataout),
    .Reg18(register32_19_dataout), .Reg19(register32_20_dataout), .Reg20(register32_21_dataout),
    .Reg1(register32_2_dataout), .Reg21(register32_22_dataout), .Reg22(register32_23_dataout),
    .Reg23(register32_24_dataout), .Reg24(register32_25_dataout), .Reg25(register32_26_dataout),
    .Reg26(register32_27_dataout), .Reg27(register32_28_dataout), .Reg28(register32_29_dataout),
    .Reg29(register32_30_dataout), .Reg30(register32_31_dataout), .Reg2(register32_3_dataout),
    .Reg31(register32_32_dataout), .Reg3(register32_4_dataout), .Reg4(register32_5_dataout),
    .DataOut(ReadData2));
endmodule

module RegisterDecoder (
  input  [4:0] RegAddr,
  output Reg0,
  output Reg1,
  output Reg2,
  output Reg3,
  output Reg4,
  output Reg5,
  output Reg6,
  output Reg7,
  output Reg8,
  output Reg9,
  output Reg10,
  output Reg11,
  output Reg12,
  output Reg13,
  output Reg14,
  output Reg15,
  output Reg16,
  output Reg17,
  output Reg18,
  output Reg19,
  output Reg20,
  output Reg21,
  output Reg22,
  output Reg23,
  output Reg24,
  output Reg25,
  output Reg26,
  output Reg27,
  output Reg28,
  output Reg29,
  output Reg30,
  output Reg31
);

  wire and_1_out, and_2_out, and_3_out, and_4_out, and_5_out, and_6_out, and_7_out, and_8_out, and_9_out,
       and_10_out, and_11_out, and_12_out, and_13_out, and_14_out, and_15_out, and_16_out, and_17_out,
       and_18_out, and_19_out, and_20_out, and_21_out, and_22_out, and_23_out, and_24_out, and_25_out,
       and_26_out, and_27_out, and_28_out, and_29_out, and_30_out, and_31_out, and_32_out, and_33_out,
       and_34_out, and_35_out, and_36_out, and_37_out, and_38_out, and_39_out, and_40_out, and_41_out,
       and_42_out, and_43_out, and_44_out, and_45_out, and_46_out, and_47_out, and_48_out, and_49_out,
       and_50_out, and_51_out, and_52_out, and_53_out, and_54_out, and_55_out, and_56_out, and_57_out,
       and_58_out, and_59_out, and_60_out, and_61_out, and_62_out, and_63_out, and_64_out, and_65_out,
       and_66_out, and_67_out, and_68_out, and_69_out, and_70_out, and_71_out, and_72_out, and_73_out,
       and_74_out, and_75_out, and_76_out, and_77_out, and_78_out, and_79_out, and_80_out, and_81_out,
       and_82_out, and_83_out, and_84_out, and_85_out, and_86_out, and_87_out, and_88_out, and_89_out,
       and_90_out, and_91_out, and_92_out, and_93_out, and_94_out, and_95_out, and_96_out, not_1_out,
       not_2_out, not_3_out, not_4_out, not_5_out, not_6_out, not_7_out, not_8_out, not_9_out, not_10_out,
       not_11_out, not_12_out, not_13_out, not_14_out, not_15_out, not_16_out, not_17_out, not_18_out,
       not_19_out, not_20_out, not_21_out, not_22_out, not_23_out, not_24_out, not_25_out, not_26_out,
       not_27_out, not_28_out, not_29_out, not_30_out, not_31_out, not_32_out, not_33_out, not_34_out,
       not_35_out, not_36_out, not_37_out, not_38_out, not_39_out, not_40_out, not_41_out, not_42_out,
       not_43_out, not_44_out, not_45_out, not_46_out, not_47_out, not_48_out, not_49_out, not_50_out,
       not_51_out, not_52_out, not_53_out, not_54_out, not_55_out, not_56_out, not_57_out, not_58_out,
       not_59_out, not_60_out, not_61_out, not_62_out, not_63_out, not_64_out, not_65_out, not_66_out,
       not_67_out, not_68_out, not_69_out, not_70_out, not_71_out, not_72_out, not_73_out, not_74_out,
       not_75_out, not_76_out, not_77_out, not_78_out, not_79_out, not_80_out;

  not not_1 (not_1_out, RegAddr[0]);
  not not_2 (not_2_out, RegAddr[1]);
  not not_3 (not_3_out, RegAddr[2]);
  not not_4 (not_4_out, RegAddr[3]);
  not not_5 (not_5_out, RegAddr[4]);
  not not_6 (not_6_out, RegAddr[1]);
  not not_7 (not_7_out, RegAddr[2]);
  not not_8 (not_8_out, RegAddr[3]);
  not not_9 (not_9_out, RegAddr[4]);
  not not_10 (not_10_out, RegAddr[0]);
  not not_11 (not_11_out, RegAddr[2]);
  not not_12 (not_12_out, RegAddr[3]);
  not not_13 (not_13_out, RegAddr[4]);
  not not_14 (not_14_out, RegAddr[2]);
  not not_15 (not_15_out, RegAddr[3]);
  not not_16 (not_16_out, RegAddr[4]);
  not not_17 (not_17_out, RegAddr[0]);
  not not_18 (not_18_out, RegAddr[1]);
  not not_19 (not_19_out, RegAddr[3]);
  not not_20 (not_20_out, RegAddr[4]);
  not not_21 (not_21_out, RegAddr[1]);
  not not_22 (not_22_out, RegAddr[3]);
  not not_23 (not_23_out, RegAddr[4]);
  not not_24 (not_24_out, RegAddr[0]);
  not not_25 (not_25_out, RegAddr[3]);
  not not_26 (not_26_out, RegAddr[4]);
  not not_27 (not_27_out, RegAddr[3]);
  not not_28 (not_28_out, RegAddr[4]);
  not not_29 (not_29_out, RegAddr[0]);
  not not_30 (not_30_out, RegAddr[1]);
  not not_31 (not_31_out, RegAddr[2]);
  not not_32 (not_32_out, RegAddr[4]);
  not not_33 (not_33_out, RegAddr[1]);
  not not_34 (not_34_out, RegAddr[2]);
  not not_35 (not_35_out, RegAddr[4]);
  not not_36 (not_36_out, RegAddr[0]);
  not not_37 (not_37_out, RegAddr[2]);
  not not_38 (not_38_out, RegAddr[4]);
  not not_39 (not_39_out, RegAddr[2]);
  not not_40 (not_40_out, RegAddr[4]);
  not not_41 (not_41_out, RegAddr[0]);
  not not_42 (not_42_out, RegAddr[1]);
  not not_43 (not_43_out, RegAddr[4]);
  not not_44 (not_44_out, RegAddr[1]);
  not not_45 (not_45_out, RegAddr[4]);
  not not_46 (not_46_out, RegAddr[0]);
  not not_47 (not_47_out, RegAddr[4]);
  not not_48 (not_48_out, RegAddr[4]);
  not not_49 (not_49_out, RegAddr[0]);
  not not_50 (not_50_out, RegAddr[1]);
  not not_51 (not_51_out, RegAddr[2]);
  not not_52 (not_52_out, RegAddr[3]);
  not not_53 (not_53_out, RegAddr[1]);
  not not_54 (not_54_out, RegAddr[2]);
  not not_55 (not_55_out, RegAddr[3]);
  not not_56 (not_56_out, RegAddr[0]);
  not not_57 (not_57_out, RegAddr[2]);
  not not_58 (not_58_out, RegAddr[3]);
  not not_59 (not_59_out, RegAddr[2]);
  not not_60 (not_60_out, RegAddr[3]);
  not not_61 (not_61_out, RegAddr[0]);
  not not_62 (not_62_out, RegAddr[1]);
  not not_63 (not_63_out, RegAddr[3]);
  not not_64 (not_64_out, RegAddr[1]);
  not not_65 (not_65_out, RegAddr[3]);
  not not_66 (not_66_out, RegAddr[0]);
  not not_67 (not_67_out, RegAddr[3]);
  not not_68 (not_68_out, RegAddr[3]);
  not not_69 (not_69_out, RegAddr[0]);
  not not_70 (not_70_out, RegAddr[1]);
  not not_71 (not_71_out, RegAddr[2]);
  not not_72 (not_72_out, RegAddr[1]);
  not not_73 (not_73_out, RegAddr[2]);
  not not_74 (not_74_out, RegAddr[0]);
  not not_75 (not_75_out, RegAddr[2]);
  not not_76 (not_76_out, RegAddr[2]);
  not not_77 (not_77_out, RegAddr[0]);
  not not_78 (not_78_out, RegAddr[1]);
  not not_79 (not_79_out, RegAddr[1]);
  not not_80 (not_80_out, RegAddr[0]);
  and and_1 (and_1_out, not_2_out, not_3_out);
  and and_2 (and_2_out, not_4_out, not_5_out);
  and and_3 (and_3_out, not_6_out, not_7_out);
  and and_4 (and_4_out, not_8_out, not_9_out);
  and and_5 (and_5_out, RegAddr[1], not_11_out);
  and and_6 (and_6_out, not_12_out, not_13_out);
  and and_7 (and_7_out, RegAddr[1], not_14_out);
  and and_8 (and_8_out, not_15_out, not_16_out);
  and and_9 (and_9_out, not_18_out, RegAddr[2]);
  and and_10 (and_10_out, not_19_out, not_20_out);
  and and_11 (and_11_out, not_21_out, RegAddr[2]);
  and and_12 (and_12_out, not_22_out, not_23_out);
  and and_13 (and_13_out, RegAddr[1], RegAddr[2]);
  and and_14 (and_14_out, not_25_out, not_26_out);
  and and_15 (and_15_out, RegAddr[1], RegAddr[2]);
  and and_16 (and_16_out, not_27_out, not_28_out);
  and and_17 (and_17_out, not_30_out, not_31_out);
  and and_18 (and_18_out, RegAddr[3], not_32_out);
  and and_19 (and_19_out, not_33_out, not_34_out);
  and and_20 (and_20_out, RegAddr[3], not_35_out);
  and and_21 (and_21_out, RegAddr[1], not_37_out);
  and and_22 (and_22_out, RegAddr[3], not_38_out);
  and and_23 (and_23_out, RegAddr[1], not_39_out);
  and and_24 (and_24_out, RegAddr[3], not_40_out);
  and and_25 (and_25_out, not_42_out, RegAddr[2]);
  and and_26 (and_26_out, RegAddr[3], not_43_out);
  and and_27 (and_27_out, not_44_out, RegAddr[2]);
  and and_28 (and_28_out, RegAddr[3], not_45_out);
  and and_29 (and_29_out, RegAddr[1], RegAddr[2]);
  and and_30 (and_30_out, RegAddr[3], not_47_out);
  and and_31 (and_31_out, RegAddr[1], RegAddr[2]);
  and and_32 (and_32_out, RegAddr[3], not_48_out);
  and and_33 (and_33_out, not_50_out, not_51_out);
  and and_34 (and_34_out, not_52_out, RegAddr[4]);
  and and_35 (and_35_out, not_53_out, not_54_out);
  and and_36 (and_36_out, not_55_out, RegAddr[4]);
  and and_37 (and_37_out, RegAddr[1], not_57_out);
  and and_38 (and_38_out, not_58_out, RegAddr[4]);
  and and_39 (and_39_out, RegAddr[1], not_59_out);
  and and_40 (and_40_out, not_60_out, RegAddr[4]);
  and and_41 (and_41_out, not_62_out, RegAddr[2]);
  and and_42 (and_42_out, not_63_out, RegAddr[4]);
  and and_43 (and_43_out, not_64_out, RegAddr[2]);
  and and_44 (and_44_out, not_65_out, RegAddr[4]);
  and and_45 (and_45_out, RegAddr[1], RegAddr[2]);
  and and_46 (and_46_out, not_67_out, RegAddr[4]);
  and and_47 (and_47_out, RegAddr[1], RegAddr[2]);
  and and_48 (and_48_out, not_68_out, RegAddr[4]);
  and and_49 (and_49_out, not_70_out, not_71_out);
  and and_50 (and_50_out, RegAddr[3], RegAddr[4]);
  and and_51 (and_51_out, not_72_out, not_73_out);
  and and_52 (and_52_out, RegAddr[3], RegAddr[4]);
  and and_53 (and_53_out, RegAddr[1], not_75_out);
  and and_54 (and_54_out, RegAddr[3], RegAddr[4]);
  and and_55 (and_55_out, RegAddr[1], not_76_out);
  and and_56 (and_56_out, RegAddr[3], RegAddr[4]);
  and and_57 (and_57_out, not_78_out, RegAddr[2]);
  and and_58 (and_58_out, RegAddr[3], RegAddr[4]);
  and and_59 (and_59_out, not_79_out, RegAddr[2]);
  and and_60 (and_60_out, RegAddr[3], RegAddr[4]);
  and and_61 (and_61_out, RegAddr[1], RegAddr[2]);
  and and_62 (and_62_out, RegAddr[3], RegAddr[4]);
  and and_63 (and_63_out, RegAddr[1], RegAddr[2]);
  and and_64 (and_64_out, RegAddr[3], RegAddr[4]);
  and and_65 (and_65_out, and_1_out, and_2_out);
  and and_66 (and_66_out, and_3_out, and_4_out);
  and and_67 (and_67_out, and_5_out, and_6_out);
  and and_68 (and_68_out, and_7_out, and_8_out);
  and and_69 (and_69_out, and_9_out, and_10_out);
  and and_70 (and_70_out, and_11_out, and_12_out);
  and and_71 (and_71_out, and_13_out, and_14_out);
  and and_72 (and_72_out, and_15_out, and_16_out);
  and and_73 (and_73_out, and_17_out, and_18_out);
  and and_74 (and_74_out, and_19_out, and_20_out);
  and and_75 (and_75_out, and_21_out, and_22_out);
  and and_76 (and_76_out, and_23_out, and_24_out);
  and and_77 (and_77_out, and_25_out, and_26_out);
  and and_78 (and_78_out, and_27_out, and_28_out);
  and and_79 (and_79_out, and_29_out, and_30_out);
  and and_80 (and_80_out, and_31_out, and_32_out);
  and and_81 (and_81_out, and_33_out, and_34_out);
  and and_82 (and_82_out, and_35_out, and_36_out);
  and and_83 (and_83_out, and_37_out, and_38_out);
  and and_84 (and_84_out, and_39_out, and_40_out);
  and and_85 (and_85_out, and_41_out, and_42_out);
  and and_86 (and_86_out, and_43_out, and_44_out);
  and and_87 (and_87_out, and_45_out, and_46_out);
  and and_88 (and_88_out, and_47_out, and_48_out);
  and and_89 (and_89_out, and_49_out, and_50_out);
  and and_90 (and_90_out, and_51_out, and_52_out);
  and and_91 (and_91_out, and_53_out, and_54_out);
  and and_92 (and_92_out, and_55_out, and_56_out);
  and and_93 (and_93_out, and_57_out, and_58_out);
  and and_94 (and_94_out, and_59_out, and_60_out);
  and and_95 (and_95_out, and_61_out, and_62_out);
  and and_96 (and_96_out, and_63_out, and_64_out);
  and and_97 (Reg0, not_1_out, and_65_out);
  and and_98 (Reg1, RegAddr[0], and_66_out);
  and and_99 (Reg2, not_10_out, and_67_out);
  and and_100 (Reg3, RegAddr[0], and_68_out);
  and and_101 (Reg4, not_17_out, and_69_out);
  and and_102 (Reg5, RegAddr[0], and_70_out);
  and and_103 (Reg6, not_24_out, and_71_out);
  and and_104 (Reg7, RegAddr[0], and_72_out);
  and and_105 (Reg8, not_29_out, and_73_out);
  and and_106 (Reg9, RegAddr[0], and_74_out);
  and and_107 (Reg10, not_36_out, and_75_out);
  and and_108 (Reg11, RegAddr[0], and_76_out);
  and and_109 (Reg12, not_41_out, and_77_out);
  and and_110 (Reg13, RegAddr[0], and_78_out);
  and and_111 (Reg14, not_46_out, and_79_out);
  and and_112 (Reg15, RegAddr[0], and_80_out);
  and and_113 (Reg16, not_49_out, and_81_out);
  and and_114 (Reg17, RegAddr[0], and_82_out);
  and and_115 (Reg18, not_56_out, and_83_out);
  and and_116 (Reg19, RegAddr[0], and_84_out);
  and and_117 (Reg20, not_61_out, and_85_out);
  and and_118 (Reg21, RegAddr[0], and_86_out);
  and and_119 (Reg22, not_66_out, and_87_out);
  and and_120 (Reg23, RegAddr[0], and_88_out);
  and and_121 (Reg24, not_69_out, and_89_out);
  and and_122 (Reg25, RegAddr[0], and_90_out);
  and and_123 (Reg26, not_74_out, and_91_out);
  and and_124 (Reg27, RegAddr[0], and_92_out);
  and and_125 (Reg28, not_77_out, and_93_out);
  and and_126 (Reg29, RegAddr[0], and_94_out);
  and and_127 (Reg30, not_80_out, and_95_out);
  and and_128 (Reg31, RegAddr[0], and_96_out);
endmodule

module RegisterMux (
  input  [31:0] Reg0,
  input  [31:0] Reg1,
  input  [31:0] Reg2,
  input  [31:0] Reg3,
  input  [31:0] Reg4,
  input  [31:0] Reg5,
  input  [31:0] Reg6,
  input  [31:0] Reg7,
  input  [31:0] Reg8,
  input  [31:0] Reg9,
  input  [31:0] Reg10,
  input  [31:0] Reg11,
  input  [31:0] Reg12,
  input  [31:0] Reg13,
  input  [31:0] Reg14,
  input  [31:0] Reg15,
  input  [31:0] Reg16,
  input  [31:0] Reg17,
  input  [31:0] Reg18,
  input  [31:0] Reg19,
  input  [31:0] Reg20,
  input  [31:0] Reg21,
  input  [31:0] Reg22,
  input  [31:0] Reg23,
  input  [31:0] Reg24,
  input  [31:0] Reg25,
  input  [31:0] Reg26,
  input  [31:0] Reg27,
  input  [31:0] Reg28,
  input  [31:0] Reg29,
  input  [31:0] Reg30,
  input  [31:0] Reg31,
  input  [4:0] RegAddr,
  output [31:0] DataOut
);

  wire and_1_out, and_2_out, and_3_out, and_4_out, and_5_out, and_6_out, and_7_out, and_8_out, and_9_out,
       and_10_out, and_11_out, and_12_out, and_13_out, and_14_out, and_15_out, and_16_out, and_17_out,
       and_18_out, and_19_out, and_20_out, and_21_out, and_22_out, and_23_out, and_24_out, and_25_out,
       and_26_out, and_27_out, and_28_out, and_29_out, and_30_out, and_31_out, and_32_out, and_33_out,
       and_34_out, and_35_out, and_36_out, and_37_out, and_38_out, and_39_out, and_40_out, and_41_out,
       and_42_out, and_43_out, and_44_out, and_45_out, and_46_out, and_47_out, and_48_out, and_49_out,
       and_50_out, and_51_out, and_52_out, and_53_out, and_54_out, and_55_out, and_56_out, and_57_out,
       and_58_out, and_59_out, and_60_out, and_61_out, and_62_out, and_63_out, and_64_out, and_65_out,
       and_66_out, and_67_out, and_68_out, and_69_out, and_70_out, and_71_out, and_72_out, and_73_out,
       and_74_out, and_75_out, and_76_out, and_77_out, and_78_out, and_79_out, and_80_out, and_81_out,
       and_82_out, and_83_out, and_84_out, and_85_out, and_86_out, and_87_out, and_88_out, and_89_out,
       and_90_out, and_91_out, and_92_out, and_93_out, and_94_out, and_95_out, and_96_out, not_1_out,
       not_2_out, not_3_out, not_4_out, not_5_out, not_6_out, not_7_out, not_8_out, not_9_out, not_10_out,
       not_11_out, not_12_out, not_13_out, not_14_out, not_15_out, not_16_out, not_17_out, not_18_out,
       not_19_out, not_20_out, not_21_out, not_22_out, not_23_out, not_24_out, not_25_out, not_26_out,
       not_27_out, not_28_out, not_29_out, not_30_out, not_31_out, not_32_out, not_33_out, not_34_out,
       not_35_out, not_36_out, not_37_out, not_38_out, not_39_out, not_40_out, not_41_out, not_42_out,
       not_43_out, not_44_out, not_45_out, not_46_out, not_47_out, not_48_out, not_49_out, not_50_out,
       not_51_out, not_52_out, not_53_out, not_54_out, not_55_out, not_56_out, not_57_out, not_58_out,
       not_59_out, not_60_out, not_61_out, not_62_out, not_63_out, not_64_out, not_65_out, not_66_out,
       not_67_out, not_68_out, not_69_out, not_70_out, not_71_out, not_72_out, not_73_out, not_74_out,
       not_75_out, not_76_out, not_77_out, not_78_out, not_79_out, not_80_out;
  wire [31:0] and_129_out, and_130_out, and_131_out, and_132_out, and_133_out, and_134_out, and_135_out,
       and_136_out, and_137_out, and_138_out, and_139_out, and_140_out, and_141_out, and_142_out,
       and_143_out, and_144_out, and_145_out, and_146_out, and_147_out, and_148_out, and_149_out,
       and_150_out, and_151_out, and_152_out, and_153_out, and_154_out, and_155_out, and_156_out,
       and_157_out, and_158_out, and_159_out, and_160_out, or_1_out, or_2_out, or_3_out, or_4_out, or_5_out,
       or_6_out, or_7_out, or_8_out, or_9_out, or_10_out, or_11_out, or_12_out, or_13_out, or_14_out,
       or_15_out, or_16_out, or_17_out, or_18_out, or_19_out, or_20_out, or_21_out, or_22_out, or_23_out,
       or_24_out, or_25_out, or_26_out, or_27_out, or_28_out, or_29_out, or_30_out;
  wire [31:31] and_97_out, and_98_out, and_99_out, and_100_out, and_101_out, and_102_out, and_103_out,
       and_104_out, and_105_out, and_106_out, and_107_out, and_108_out, and_109_out, and_110_out,
       and_111_out, and_112_out, and_113_out, and_114_out, and_115_out, and_116_out, and_117_out,
       and_118_out, and_119_out, and_120_out, and_121_out, and_122_out, and_123_out, and_124_out,
       and_125_out, and_126_out, and_127_out, and_128_out;

  not not_1 (not_1_out, RegAddr[0]);
  not not_2 (not_2_out, RegAddr[1]);
  not not_3 (not_3_out, RegAddr[2]);
  not not_4 (not_4_out, RegAddr[3]);
  not not_5 (not_5_out, RegAddr[4]);
  not not_6 (not_6_out, RegAddr[1]);
  not not_7 (not_7_out, RegAddr[2]);
  not not_8 (not_8_out, RegAddr[3]);
  not not_9 (not_9_out, RegAddr[4]);
  not not_10 (not_10_out, RegAddr[0]);
  not not_11 (not_11_out, RegAddr[2]);
  not not_12 (not_12_out, RegAddr[3]);
  not not_13 (not_13_out, RegAddr[4]);
  not not_14 (not_14_out, RegAddr[2]);
  not not_15 (not_15_out, RegAddr[3]);
  not not_16 (not_16_out, RegAddr[4]);
  not not_17 (not_17_out, RegAddr[0]);
  not not_18 (not_18_out, RegAddr[1]);
  not not_19 (not_19_out, RegAddr[3]);
  not not_20 (not_20_out, RegAddr[4]);
  not not_21 (not_21_out, RegAddr[1]);
  not not_22 (not_22_out, RegAddr[3]);
  not not_23 (not_23_out, RegAddr[4]);
  not not_24 (not_24_out, RegAddr[0]);
  not not_25 (not_25_out, RegAddr[3]);
  not not_26 (not_26_out, RegAddr[4]);
  not not_27 (not_27_out, RegAddr[3]);
  not not_28 (not_28_out, RegAddr[4]);
  not not_29 (not_29_out, RegAddr[0]);
  not not_30 (not_30_out, RegAddr[1]);
  not not_31 (not_31_out, RegAddr[2]);
  not not_32 (not_32_out, RegAddr[4]);
  not not_33 (not_33_out, RegAddr[1]);
  not not_34 (not_34_out, RegAddr[2]);
  not not_35 (not_35_out, RegAddr[4]);
  not not_36 (not_36_out, RegAddr[0]);
  not not_37 (not_37_out, RegAddr[2]);
  not not_38 (not_38_out, RegAddr[4]);
  not not_39 (not_39_out, RegAddr[2]);
  not not_40 (not_40_out, RegAddr[4]);
  not not_41 (not_41_out, RegAddr[0]);
  not not_42 (not_42_out, RegAddr[1]);
  not not_43 (not_43_out, RegAddr[4]);
  not not_44 (not_44_out, RegAddr[1]);
  not not_45 (not_45_out, RegAddr[4]);
  not not_46 (not_46_out, RegAddr[0]);
  not not_47 (not_47_out, RegAddr[4]);
  not not_48 (not_48_out, RegAddr[4]);
  not not_49 (not_49_out, RegAddr[0]);
  not not_50 (not_50_out, RegAddr[1]);
  not not_51 (not_51_out, RegAddr[2]);
  not not_52 (not_52_out, RegAddr[3]);
  not not_53 (not_53_out, RegAddr[1]);
  not not_54 (not_54_out, RegAddr[2]);
  not not_55 (not_55_out, RegAddr[3]);
  not not_56 (not_56_out, RegAddr[0]);
  not not_57 (not_57_out, RegAddr[2]);
  not not_58 (not_58_out, RegAddr[3]);
  not not_59 (not_59_out, RegAddr[2]);
  not not_60 (not_60_out, RegAddr[3]);
  not not_61 (not_61_out, RegAddr[0]);
  not not_62 (not_62_out, RegAddr[1]);
  not not_63 (not_63_out, RegAddr[3]);
  not not_64 (not_64_out, RegAddr[1]);
  not not_65 (not_65_out, RegAddr[3]);
  not not_66 (not_66_out, RegAddr[0]);
  not not_67 (not_67_out, RegAddr[3]);
  not not_68 (not_68_out, RegAddr[3]);
  not not_69 (not_69_out, RegAddr[0]);
  not not_70 (not_70_out, RegAddr[1]);
  not not_71 (not_71_out, RegAddr[2]);
  not not_72 (not_72_out, RegAddr[1]);
  not not_73 (not_73_out, RegAddr[2]);
  not not_74 (not_74_out, RegAddr[0]);
  not not_75 (not_75_out, RegAddr[2]);
  not not_76 (not_76_out, RegAddr[2]);
  not not_77 (not_77_out, RegAddr[0]);
  not not_78 (not_78_out, RegAddr[1]);
  not not_79 (not_79_out, RegAddr[1]);
  not not_80 (not_80_out, RegAddr[0]);
  and and_1 (and_1_out, not_2_out, not_3_out);
  and and_2 (and_2_out, not_4_out, not_5_out);
  and and_3 (and_3_out, not_6_out, not_7_out);
  and and_4 (and_4_out, not_8_out, not_9_out);
  and and_5 (and_5_out, RegAddr[1], not_11_out);
  and and_6 (and_6_out, not_12_out, not_13_out);
  and and_7 (and_7_out, RegAddr[1], not_14_out);
  and and_8 (and_8_out, not_15_out, not_16_out);
  and and_9 (and_9_out, not_18_out, RegAddr[2]);
  and and_10 (and_10_out, not_19_out, not_20_out);
  and and_11 (and_11_out, not_21_out, RegAddr[2]);
  and and_12 (and_12_out, not_22_out, not_23_out);
  and and_13 (and_13_out, RegAddr[1], RegAddr[2]);
  and and_14 (and_14_out, not_25_out, not_26_out);
  and and_15 (and_15_out, RegAddr[1], RegAddr[2]);
  and and_16 (and_16_out, not_27_out, not_28_out);
  and and_17 (and_17_out, not_30_out, not_31_out);
  and and_18 (and_18_out, RegAddr[3], not_32_out);
  and and_19 (and_19_out, not_33_out, not_34_out);
  and and_20 (and_20_out, RegAddr[3], not_35_out);
  and and_21 (and_21_out, RegAddr[1], not_37_out);
  and and_22 (and_22_out, RegAddr[3], not_38_out);
  and and_23 (and_23_out, RegAddr[1], not_39_out);
  and and_24 (and_24_out, RegAddr[3], not_40_out);
  and and_25 (and_25_out, not_42_out, RegAddr[2]);
  and and_26 (and_26_out, RegAddr[3], not_43_out);
  and and_27 (and_27_out, not_44_out, RegAddr[2]);
  and and_28 (and_28_out, RegAddr[3], not_45_out);
  and and_29 (and_29_out, RegAddr[1], RegAddr[2]);
  and and_30 (and_30_out, RegAddr[3], not_47_out);
  and and_31 (and_31_out, RegAddr[1], RegAddr[2]);
  and and_32 (and_32_out, RegAddr[3], not_48_out);
  and and_33 (and_33_out, not_50_out, not_51_out);
  and and_34 (and_34_out, not_52_out, RegAddr[4]);
  and and_35 (and_35_out, not_53_out, not_54_out);
  and and_36 (and_36_out, not_55_out, RegAddr[4]);
  and and_37 (and_37_out, RegAddr[1], not_57_out);
  and and_38 (and_38_out, not_58_out, RegAddr[4]);
  and and_39 (and_39_out, RegAddr[1], not_59_out);
  and and_40 (and_40_out, not_60_out, RegAddr[4]);
  and and_41 (and_41_out, not_62_out, RegAddr[2]);
  and and_42 (and_42_out, not_63_out, RegAddr[4]);
  and and_43 (and_43_out, not_64_out, RegAddr[2]);
  and and_44 (and_44_out, not_65_out, RegAddr[4]);
  and and_45 (and_45_out, RegAddr[1], RegAddr[2]);
  and and_46 (and_46_out, not_67_out, RegAddr[4]);
  and and_47 (and_47_out, RegAddr[1], RegAddr[2]);
  and and_48 (and_48_out, not_68_out, RegAddr[4]);
  and and_49 (and_49_out, not_70_out, not_71_out);
  and and_50 (and_50_out, RegAddr[3], RegAddr[4]);
  and and_51 (and_51_out, not_72_out, not_73_out);
  and and_52 (and_52_out, RegAddr[3], RegAddr[4]);
  and and_53 (and_53_out, RegAddr[1], not_75_out);
  and and_54 (and_54_out, RegAddr[3], RegAddr[4]);
  and and_55 (and_55_out, RegAddr[1], not_76_out);
  and and_56 (and_56_out, RegAddr[3], RegAddr[4]);
  and and_57 (and_57_out, not_78_out, RegAddr[2]);
  and and_58 (and_58_out, RegAddr[3], RegAddr[4]);
  and and_59 (and_59_out, not_79_out, RegAddr[2]);
  and and_60 (and_60_out, RegAddr[3], RegAddr[4]);
  and and_61 (and_61_out, RegAddr[1], RegAddr[2]);
  and and_62 (and_62_out, RegAddr[3], RegAddr[4]);
  and and_63 (and_63_out, RegAddr[1], RegAddr[2]);
  and and_64 (and_64_out, RegAddr[3], RegAddr[4]);
  and and_65 (and_65_out, and_1_out, and_2_out);
  and and_66 (and_66_out, and_3_out, and_4_out);
  and and_67 (and_67_out, and_5_out, and_6_out);
  and and_68 (and_68_out, and_7_out, and_8_out);
  and and_69 (and_69_out, and_9_out, and_10_out);
  and and_70 (and_70_out, and_11_out, and_12_out);
  and and_71 (and_71_out, and_13_out, and_14_out);
  and and_72 (and_72_out, and_15_out, and_16_out);
  and and_73 (and_73_out, and_17_out, and_18_out);
  and and_74 (and_74_out, and_19_out, and_20_out);
  and and_75 (and_75_out, and_21_out, and_22_out);
  and and_76 (and_76_out, and_23_out, and_24_out);
  and and_77 (and_77_out, and_25_out, and_26_out);
  and and_78 (and_78_out, and_27_out, and_28_out);
  and and_79 (and_79_out, and_29_out, and_30_out);
  and and_80 (and_80_out, and_31_out, and_32_out);
  and and_81 (and_81_out, and_33_out, and_34_out);
  and and_82 (and_82_out, and_35_out, and_36_out);
  and and_83 (and_83_out, and_37_out, and_38_out);
  and and_84 (and_84_out, and_39_out, and_40_out);
  and and_85 (and_85_out, and_41_out, and_42_out);
  and and_86 (and_86_out, and_43_out, and_44_out);
  and and_87 (and_87_out, and_45_out, and_46_out);
  and and_88 (and_88_out, and_47_out, and_48_out);
  and and_89 (and_89_out, and_49_out, and_50_out);
  and and_90 (and_90_out, and_51_out, and_52_out);
  and and_91 (and_91_out, and_53_out, and_54_out);
  and and_92 (and_92_out, and_55_out, and_56_out);
  and and_93 (and_93_out, and_57_out, and_58_out);
  and and_94 (and_94_out, and_59_out, and_60_out);
  and and_95 (and_95_out, and_61_out, and_62_out);
  and and_96 (and_96_out, and_63_out, and_64_out);
  and and_97 (and_97_out[31], not_1_out, and_65_out);
  and and_98 (and_98_out[31], RegAddr[0], and_66_out);
  and and_99 (and_99_out[31], not_10_out, and_67_out);
  and and_100 (and_100_out[31], RegAddr[0], and_68_out);
  and and_101 (and_101_out[31], not_17_out, and_69_out);
  and and_102 (and_102_out[31], RegAddr[0], and_70_out);
  and and_103 (and_103_out[31], not_24_out, and_71_out);
  and and_104 (and_104_out[31], RegAddr[0], and_72_out);
  and and_105 (and_105_out[31], not_29_out, and_73_out);
  and and_106 (and_106_out[31], RegAddr[0], and_74_out);
  and and_107 (and_107_out[31], not_36_out, and_75_out);
  and and_108 (and_108_out[31], RegAddr[0], and_76_out);
  and and_109 (and_109_out[31], not_41_out, and_77_out);
  and and_110 (and_110_out[31], RegAddr[0], and_78_out);
  and and_111 (and_111_out[31], not_46_out, and_79_out);
  and and_112 (and_112_out[31], RegAddr[0], and_80_out);
  and and_113 (and_113_out[31], not_49_out, and_81_out);
  and and_114 (and_114_out[31], RegAddr[0], and_82_out);
  and and_115 (and_115_out[31], not_56_out, and_83_out);
  and and_116 (and_116_out[31], RegAddr[0], and_84_out);
  and and_117 (and_117_out[31], not_61_out, and_85_out);
  and and_118 (and_118_out[31], RegAddr[0], and_86_out);
  and and_119 (and_119_out[31], not_66_out, and_87_out);
  and and_120 (and_120_out[31], RegAddr[0], and_88_out);
  and and_121 (and_121_out[31], not_69_out, and_89_out);
  and and_122 (and_122_out[31], RegAddr[0], and_90_out);
  and and_123 (and_123_out[31], not_74_out, and_91_out);
  and and_124 (and_124_out[31], RegAddr[0], and_92_out);
  and and_125 (and_125_out[31], not_77_out, and_93_out);
  and and_126 (and_126_out[31], RegAddr[0], and_94_out);
  and and_127 (and_127_out[31], not_80_out, and_95_out);
  and and_128 (and_128_out[31], RegAddr[0], and_96_out);
  assign and_129_out = {32{and_97_out[31]}} & Reg0;  // AND_Gate and_129, 32 bits wide
  assign and_130_out = {32{and_98_out[31]}} & Reg1;  // AND_Gate and_130, 32 bits wide
  assign and_131_out = {32{and_99_out[31]}} & Reg2;  // AND_Gate and_131, 32 bits wide
  assign and_132_out = {32{and_100_out[31]}} & Reg3;  // AND_Gate and_132, 32 bits wide
  assign and_133_out = {32{and_101_out[31]}} & Reg4;  // AND_Gate and_133, 32 bits wide
  assign and_134_out = {32{and_102_out[31]}} & Reg5;  // AND_Gate and_134, 32 bits wide
  assign and_135_out = {32{and_103_out[31]}} & Reg6;  // AND_Gate and_135, 32 bits wide
  assign and_136_out = {32{and_104_out[31]}} & Reg7;  // AND_Gate and_136, 32 bits wide
  assign and_137_out = {32{and_105_out[31]}} & Reg8;  // AND_Gate and_137, 32 bits wide
  assign and_138_out = {32{and_106_out[31]}} & Reg9;  // AND_Gate and_138, 32 bits wide
  assign and_139_out = {32{and_107_out[31]}} & Reg10;  // AND_Gate and_139, 32 bits wide
  assign and_140_out = {32{and_108_out[31]}} & Reg11;  // AND_Gate and_140, 32 bits wide
  assign and_141_out = {32{and_109_out[31]}} & Reg12;  // AND_Gate and_141, 32 bits wide
  assign and_142_out = {32{and_110_out[31]}} & Reg13;  // AND_Gate and_142, 32 bits wide
  assign and_143_out = {32{and_111_out[31]}} & Reg14;  // AND_Gate and_143, 32 bits wide
  assign and_144_out = {32{and_112_out[31]}} & Reg15;  // AND_Gate and_144, 32 bits wide
  assign and_145_out = {32{and_113_out[31]}} & Reg16;  // AND_Gate and_145, 32 bits wide
  assign and_146_out = {32{and_114_out[31]}} & Reg17;  // AND_Gate and_146, 32 bits wide
  assign and_147_out = {32{and_115_out[31]}} & Reg18;  // AND_Gate and_147, 32 bits wide
  assign and_148_out = {32{and_116_out[31]}} & Reg19;  // AND_Gate and_148, 32 bits wide
  assign and_149_out = {32{and_117_out[31]}} & Reg20;  // AND_Gate and_149, 32 bits wide
  assign and_150_out = {32{and_118_out[31]}} & Reg21;  // AND_Gate and_150, 32 bits wide
  assign and_151_out = {32{and_119_out[31]}} & Reg22;  // AND_Gate and_151, 32 bits wide
  assign and_152_out = {32{and_120_out[31]}} & Reg23;  // AND_Gate and_152, 32 bits wide
  assign and_153_out = {32{and_121_out[31]}} & Reg24;  // AND_Gate and_153, 32 bits wide
  assign and_154_out = {32{and_122_out[31]}} & Reg25;  // AND_Gate and_154, 32 bits wide
  assign and_155_out = {32{and_123_out[31]}} & Reg26;  // AND_Gate and_155, 32 bits wide
  assign and_156_out = {32{and_124_out[31]}} & Reg27;  // AND_Gate and_156, 32 bits wide
  assign and_157_out = {32{and_125_out[31]}} & Reg28;  // AND_Gate and_157, 32 bits wide
  assign and_158_out = {32{and_126_out[31]}} & Reg29;  // AND_Gate and_158, 32 bits wide
  assign and_159_out = {32{and_127_out[31]}} & Reg30;  // AND_Gate and_159, 32 bits wide
  assign and_160_out = {32{and_128_out[31]}} & Reg31;  // AND_Gate and_160, 32 bits wide
  assign or_1_out = and_129_out | and_130_out;  // OR_Gate or_1, 32 bits wide
  assign or_2_out = and_131_out | and_132_out;  // OR_Gate or_2, 32 bits wide
  assign or_3_out = and_133_out | and_134_out;  // OR_Gate or_3, 32 bits wide
  assign or_4_out = and_135_out | and_136_out;  // OR_Gate or_4, 32 bits wide
  assign or_5_out = and_137_out | and_138_out;  // OR_Gate or_5, 32 bits wide
  assign or_6_out = and_139_out | and_140_out;  // OR_Gate or_6, 32 bits wide
  assign or_7_out = and_141_out | and_142_out;  // OR_Gate or_7, 32 bits wide
  assign or_8_out = and_143_out | and_144_out;  // OR_Gate or_8, 32 bits wide
  assign or_9_out = and_145_out | and_146_out;  // OR_Gate or_9, 32 bits wide
  assign or_10_out = and_147_out | and_148_out;  // OR_Gate or_10, 32 bits wide
  assign or_11_out = and_149_out | and_150_out;  // OR_Gate or_11, 32 bits wide
  assign or_12_out = and_151_out | and_152_out;  // OR_Gate or_12, 32 bits wide
  assign or_13_out = and_153_out | and_154_out;  // OR_Gate or_13, 32 bits wide
  assign or_14_out = and_155_out | and_156_out;  // OR_Gate or_14, 32 bits wide
  assign or_15_out = and_157_out | and_158_out;  // OR_Gate or_15, 32 bits wide
  assign or_16_out = and_159_out | and_160_out;  // OR_Gate or_16, 32 bits wide
  assign or_17_out = or_1_out | or_2_out;  // OR_Gate or_17, 32 bits wide
  assign or_18_out = or_3_out | or_4_out;  // OR_Gate or_18, 32 bits wide
  assign or_19_out = or_5_out | or_6_out;  // OR_Gate or_19, 32 bits wide
  assign or_20_out = or_7_out | or_8_out;  // OR_Gate or_20, 32 bits wide
  assign or_21_out = or_9_out | or_10_out;  // OR_Gate or_21, 32 bits wide
  assign or_22_out = or_11_out | or_12_out;  // OR_Gate or_22, 32 bits wide
  assign or_23_out = or_13_out | or_14_out;  // OR_Gate or_23, 32 bits wide
  assign or_24_out = or_15_out | or_16_out;  // OR_Gate or_24, 32 bits wide
  assign or_25_out = or_17_out | or_18_out;  // OR_Gate or_25, 32 bits wide
  assign or_26_out = or_19_out | or_20_out;  // OR_Gate or_26, 32 bits wide
  assign or_27_out = or_21_out | or_22_out;  // OR_Gate or_27, 32 bits wide
  assign or_28_out = or_23_out | or_24_out;  // OR_Gate or_28, 32 bits wide
  assign or_29_out = or_25_out | or_26_out;  // OR_Gate or_29, 32 bits wide
  assign or_30_out = or_27_out | or_28_out;  // OR_Gate or_30, 32 bits wide
  assign DataOut = or_29_out | or_30_out;  // OR_Gate or_31, 32 bits wide
endmodule

module InstructionSplitter (
  input  Clock,
  input  [31:0] Instruction,
  output [5:0] ALUControl,
  output [15:0] Immediate,
  output [4:0] WriteReg,
  output [4:0] ReadReg2,
  output [4:0] ReadReg1,
  output [5:0] Control
);

  D_Flip_Flop d_ff_1 (.D(Instruction[0]), .clk(Clock), .Q(ALUControl[0]));  // open: Qn, preset, reset
  D_Flip_Flop d_ff_2 (.D(Instruction[1]), .clk(Clock), .Q(ALUControl[1]));  // open: Qn, preset, reset
  D_Flip_Flop d_ff_3 (.D(Instruction[2]), .clk(Clock), .Q(ALUControl[2]));  // open: Qn, preset, reset
  D_Flip_Flop d_ff_4 (.D(Instruction[3]), .clk(Clock), .Q(ALUControl[3]));  // open: Qn, preset, reset
  D_Flip_Flop d_ff_5 (.D(Instruction[4]), .clk(Clock), .Q(ALUControl[4]));  // open: Qn, preset, reset
  D_Flip_Flop d_ff_6 (.D(Instruction[5]), .clk(Clock), .Q(ALUControl[5]));  // open: Qn, preset, reset
  D_Flip_Flop d_ff_7 (.D(Instruction[6]), .clk(Clock), .Q(Immediate[6]));  // open: Qn, preset, reset
  D_Flip_Flop d_ff_8 (.D(Instruction[7]), .clk(Clock), .Q(Immediate[7]));  // open: Qn, preset, reset
  D_Flip_Flop d_ff_9 (.D(Instruction[8]), .clk(Clock), .Q(Immediate[8]));  // open: Qn, preset, reset
  D_Flip_Flop d_ff_10 (.D(Instruction[9]), .clk(Clock), .Q(Immediate[9]));  // open: Qn, preset, reset
  D_Flip_Flop d_ff_11 (.D(Instruction[10]), .clk(Clock), .Q(Immediate[10]));  // open: Qn, preset, reset
  D_Flip_Flop d_ff_12 (.D(Instruction[11]), .clk(Clock), .Q(Immediate[11]));  // open: Qn, preset, reset
  D_Flip_Flop d_ff_13 (.D(Instruction[12]), .clk(Clock), .Q(Immediate[12]));  // open: Qn, preset, reset
  D_Flip_Flop d_ff_14 (.D(Instruction[13]), .clk(Clock), .Q(Immediate[13]));  // open: Qn, preset, reset
  D_Flip_Flop d_ff_15 (.D(Instruction[14]), .clk(Clock), .Q(Immediate[14]));  // open: Qn, preset, reset
  D_Flip_Flop d_ff_16 (.D(Instruction[15]), .clk(Clock), .Q(Immediate[15]));  // open: Qn, preset, reset
  D_Flip_Flop d_ff_17 (.D(Instruction[16]), .clk(Clock), .Q(ReadReg2[0]));  // open: Qn, preset, reset
  D_Flip_Flop d_ff_18 (.D(Instruction[17]), .clk(Clock), .Q(ReadReg2[1]));  // open: Qn, preset, reset
  D_Flip_Flop d_ff_19 (.D(Instruction[18]), .clk(Clock), .Q(ReadReg2[2]));  // open: Qn, preset, reset
  D_Flip_Flop d_ff_20 (.D(Instruction[19]), .clk(Clock), .Q(ReadReg2[3]));  // open: Qn, preset, reset
  D_Flip_Flop d_ff_21 (.D(Instruction[20]), .clk(Clock), .Q(ReadReg2[4]));  // open: Qn, preset, reset
  D_Flip_Flop d_ff_22 (.D(Instruction[21]), .clk(Clock), .Q(ReadReg1[0]));  // open: Qn, preset, reset
  D_Flip_Flop d_ff_23 (.D(Instruction[22]), .clk(Clock), .Q(ReadReg1[1]));  // open: Qn, preset, reset
  D_Flip_Flop d_ff_24 (.D(Instruction[23]), .clk(Clock), .Q(ReadReg1[2]));  // open: Qn, preset, reset
  D_Flip_Flop d_ff_25 (.D(Instruction[24]), .clk(Clock), .Q(ReadReg1[3]));  // open: Qn, preset, reset
  D_Flip_Flop d_ff_26 (.D(Instruction[25]), .clk(Clock), .Q(ReadReg1[4]));  // open: Qn, preset, reset
  D_Flip_Flop d_ff_27 (.D(Instruction[26]), .clk(Clock), .Q(Control[0]));  // open: Qn, preset, reset
  D_Flip_Flop d_ff_28 (.D(Instruction[27]), .clk(Clock), .Q(Control[1]));  // open: Qn, preset, reset
  D_Flip_Flop d_ff_29 (.D(Instruction[28]), .clk(Clock), .Q(Control[2]));  // open: Qn, preset, reset
  D_Flip_Flop d_ff_30 (.D(Instruction[29]), .clk(Clock), .Q(Control[3]));  // open: Qn, preset, reset
  D_Flip_Flop d_ff_31 (.D(Instruction[30]), .clk(Clock), .Q(Control[4]));  // open: Qn, preset, reset
  D_Flip_Flop d_ff_32 (.D(Instruction[31]), .clk(Clock), .Q(Control[5]));  // open: Qn, preset, reset

  assign Immediate[5:0] = ALUControl;
  assign WriteReg = Immediate[15:11];
endmodule

module RegDstMux (
  input  [4:0] Read,
  input  [4:0] Write,
  input  RegDst,
  output [4:0] RegOut
);

  wire [4:0] and_1_out, and_2_out, not_1_out;

  assign not_1_out = ~{5{RegDst}};  // NOT_Gate not_1, 5 bits wide
  assign and_1_out = Read & not_1_out;  // AND_Gate and_1, 5 bits wide
  assign and_2_out = {5{RegDst}} & Write;  // AND_Gate and_2, 5 bits wide
  assign RegOut = and_1_out | and_2_out;  // OR_Gate or_1, 5 bits wide
endmodule

module SignExtender (
  input  [15:0] In16,
  output [31:0] Out32
);


  assign Out32 = {{17{In16[15]}}, In16[14:0]};
endmodule

module DataMux (
  input  [31:0] Data1,
  input  [31:0] Data2,
  input  Source,
  output [31:0] DataOut
);

  wire [31:0] and_1_out, and_2_out, not_1_out;

  assign not_1_out = ~{32{Source}};  // NOT_Gate not_1, 32 bits wide
  assign and_1_out = Data1 & not_1_out;  // AND_Gate and_1, 32 bits wide
  assign and_2_out = {32{Source}} & Data2;  // AND_Gate and_2, 32 bits wide
  assign DataOut = and_1_out | and_2_out;  // OR_Gate or_1, 32 bits wide
endmodule

module ShiftLeft2 (
  input  [31:0] AddrIn,
  output [31:0] AddrOut
);


  assign AddrOut = {AddrIn[29:0], 2'b00};
endmodule

module ProgramCounter (
  input  Clock,
  input  [31:0] PCin,
  output [31:0] PCout
);

  D_Flip_Flop d_ff_1 (.D(PCin[0]), .clk(Clock), .Q(PCout[0]));  // open: Qn, preset, reset
  D_Flip_Flop d_ff_2 (.D(PCin[1]), .clk(Clock), .Q(PCout[1]));  // open: Qn, preset, reset
  D_Flip_Flop d_ff_3 (.D(PCin[2]), .clk(Clock), .Q(PCout[2]));  // open: Qn, preset, reset
  D_Flip_Flop d_ff_4 (.D(PCin[3]), .clk(Clock), .Q(PCout[3]));  // open: Qn, preset, reset
  D_Flip_Flop d_ff_5 (.D(PCin[4]), .clk(Clock), .Q(PCout[4]));  // open: Qn, preset, reset
  D_Flip_Flop d_ff_6 (.D(PCin[5]), .clk(Clock), .Q(PCout[5]));  // open: Qn, preset, reset
  D_Flip_Flop d_ff_7 (.D(PCin[6]), .clk(Clock), .Q(PCout[6]));  // open: Qn, preset, reset
  D_Flip_Flop d_ff_8 (.D(PCin[7]), .clk(Clock), .Q(PCout[7]));  // open: Qn, preset, reset
  D_Flip_Flop d_ff_9 (.D(PCin[8]), .clk(Clock), .Q(PCout[8]));  // open: Qn, preset, reset
  D_Flip_Flop d_ff_10 (.D(PCin[9]), .clk(Clock), .Q(PCout[9]));  // open: Qn, preset, reset
  D_Flip_Flop d_ff_11 (.D(PCin[10]), .clk(Clock), .Q(PCout[10]));  // open: Qn, preset, reset
  D_Flip_Flop d_ff_12 (.D(PCin[11]), .clk(Clock), .Q(PCout[11]));  // open: Qn, preset, reset
  D_Flip_Flop d_ff_13 (.D(PCin[12]), .clk(Clock), .Q(PCout[12]));  // open: Qn, preset, reset
  D_Flip_Flop d_ff_14 (.D(PCin[13]), .clk(Clock), .Q(PCout[13]));  // open: Qn, preset, reset
  D_Flip_Flop d_ff_15 (.D(PCin[14]), .clk(Clock), .Q(PCout[14]));  // open: Qn, preset, reset
  D_Flip_Flop d_ff_16 (.D(PCin[15]), .clk(Clock), .Q(PCout[15]));  // open: Qn, preset, reset
  D_Flip_Flop d_ff_17 (.D(PCin[16]), .clk(Clock), .Q(PCout[16]));  // open: Qn, preset, reset
  D_Flip_Flop d_ff_18 (.D(PCin[17]), .clk(Clock), .Q(PCout[17]));  // open: Qn, preset, reset
  D_Flip_Flop d_ff_19 (.D(PCin[18]), .clk(Clock), .Q(PCout[18]));  // open: Qn, preset, reset
  D_Flip_Flop d_ff_20 (.D(PCin[19]), .clk(Clock), .Q(PCout[19]));  // open: Qn, preset, reset
  D_Flip_Flop d_ff_21 (.D(PCin[20]), .clk(Clock), .Q(PCout[20]));  // open: Qn, preset, reset
  D_Flip_Flop d_ff_22 (.D(PCin[21]), .clk(Clock), .Q(PCout[21]));  // open: Qn, preset, reset
  D_Flip_Flop d_ff_23 (.D(PCin[22]), .clk(Clock), .Q(PCout[22]));  // open: Qn, preset, reset
  D_Flip_Flop d_ff_24 (.D(PCin[23]), .clk(Clock), .Q(PCout[23]));  // open: Qn, preset, reset
  D_Flip_Flop d_ff_25 (.D(PCin[24]), .clk(Clock), .Q(PCout[24]));  // open: Qn, preset, reset
  D_Flip_Flop d_ff_26 (.D(PCin[25]), .clk(Clock), .Q(PCout[25]));  // open: Qn, preset, reset
  D_Flip_Flop d_ff_27 (.D(PCin[26]), .clk(Clock), .Q(PCout[26]));  // open: Qn, preset, reset
  D_Flip_Flop d_ff_28 (.D(PCin[27]), .clk(Clock), .Q(PCout[27]));  // open: Qn, preset, reset
  D_Flip_Flop d_ff_29 (.D(PCin[28]), .clk(Clock), .Q(PCout[28]));  // open: Qn, preset, reset
  D_Flip_Flop d_ff_30 (.D(PCin[29]), .clk(Clock), .Q(PCout[29]));  // open: Qn, preset, reset
  D_Flip_Flop d_ff_31 (.D(PCin[30]), .clk(Clock), .Q(PCout[30]));  // open: Qn, preset, reset
  D_Flip_Flop d_ff_32 (.D(PCin[31]), .clk(Clock), .Q(PCout[31]));  // open: Qn, preset, reset
endmodule

module SignShrinker (
  input  [31:0] In32,
  output [15:0] Out16
);


  assign Out16 = In32[15:0];
endmodule

module PCfix (
  input  Clock,
  input  [31:0] PCin,
  output [31:0] PCout
);

  wire not_1_out;
  wire [31:0] register32_1_dataout;

  not not_1 (not_1_out, Clock);
  Register32 register32_1 (.DataIn(PCin), .Clock(not_1_out), .DataOut(register32_1_dataout));
  Register32 register32_2 (.DataIn(register32_1_dataout), .Clock(Clock), .DataOut(PCout));
endmodule
